// Logisim project ALU_D19.circ as structural Verilog
module ALU (
  input  [2:0] S,
  input  [3:0] A,
  input  [3:0] B,
  output C0,
  output C1,
  output C2,
  output C3,
  output C4,
  output C5,
  output [3:0] Salida,
  output Carry,
  output Borrow
);

  wire [1:0] undriven, undriven_2, undriven_3;
  wire [3:0] demultiplexer_1_out0, demultiplexer_1_out1, demultiplexer_1_out2, demultiplexer_1_out4,
       demultiplexer_1_out5, demultiplexer_1_out6, demultiplexer_2_out0, demultiplexer_2_out1,
       demultiplexer_2_out4, demultiplexer_2_out5, demultiplexer_2_out6;

  Demultiplexer #(.select(3), .width(4)) demultiplexer_1 (
    .out0(demultiplexer_1_out0), .out1(demultiplexer_1_out1), .out2(demultiplexer_1_out2),
    .out4(demultiplexer_1_out4), .out5(demultiplexer_1_out5), .out6(demultiplexer_1_out6), .in(A), .sel(S));  // open: out3, out7
  Demultiplexer #(.select(3), .width(4)) demultiplexer_2 (
    .out0(demultiplexer_2_out0), .out1(demultiplexer_2_out1), .out3(demultiplexer_1_out2),
    .out4(demultiplexer_2_out4), .out5(demultiplexer_2_out5), .out6(demultiplexer_2_out6), .in(B), .sel(S));  // open: out2, out7
  ComparadorCompleto comparadorcompleto_1 (
    .A(A), .B(B), .out_3(C0), .out_4(C1), .out_5(C2), .out_6(C3), .out_7(C4), .out_8(C5));
  Sumador sumador_1 (.A(demultiplexer_1_out0), .B(demultiplexer_2_out0), .SUMA(Salida), .CARRY(Carry));
  Restador restador_1 (.A(demultiplexer_1_out1), .B(demultiplexer_2_out1), .D(Salida), .Borrow(Borrow));
  ComplementoALaBase complementoalabase_1 (.A(demultiplexer_1_out2), .Cb(Salida));  // open: Signo
  DesplazaDerecha desplazaderecha_1 (.Cantidad(undriven), .Dato(demultiplexer_1_out4), .Salida(Salida));
  DesplazaDerechaAritmetico desplazaderechaaritmetico_1 (
    .Cantidad(undriven_2), .Dato(demultiplexer_1_out5), .Salida(Salida));
  DesplazaIzquierda desplazaizquierda_1 (.Cantidad(undriven_3), .Dato(demultiplexer_1_out6), .Salida(Salida));
endmodule

module HalfAdder (
  input  B,
  input  A,
  output Carry,
  output Sum
);

  and and_1 (Carry, A, B);
  xor xor_1 (Sum, A, B);
endmodule

module FullAdder (
  input  CarryIn,
  input  B,
  input  A,
  output CarryOut,
  output Sum
);

  wire and_1_out, and_2_out, and_3_out, xor_1_out;

  and and_1 (and_1_out, A, B);
  and and_2 (and_2_out, A, CarryIn);
  and and_3 (and_3_out, B, CarryIn);
  xor xor_1 (xor_1_out, A, B);
  xor xor_2 (Sum, xor_1_out, CarryIn);
  or or_1 (CarryOut, and_1_out, and_2_out, and_3_out);
endmodule

module Sumador (
  input  [3:0] A,
  input  [3:0] B,
  output [3:0] SUMA,
  output CARRY
);

  wire fulladder_1_carryout, fulladder_2_carryout, halfadder_1_carry;

  HalfAdder halfadder_1 (.B(B[0]), .A(A[0]), .Carry(halfadder_1_carry), .Sum(SUMA[0]));
  FullAdder fulladder_1 (
    .CarryIn(halfadder_1_carry), .B(B[1]), .A(A[1]), .CarryOut(fulladder_1_carryout), .Sum(SUMA[1]));
  FullAdder fulladder_2 (
    .CarryIn(fulladder_1_carryout), .B(B[2]), .A(A[2]), .CarryOut(fulladder_2_carryout), .Sum(SUMA[2]));
  FullAdder fulladder_3 (.CarryIn(fulladder_2_carryout), .B(B[3]), .A(A[3]), .CarryOut(CARRY), .Sum(SUMA[3]));
endmodule

module Restador (
  input  [3:0] A,
  input  [3:0] B,
  output [3:0] D,
  output Borrow
);

  wire restadorcompleto_1_bout, restadorcompleto_2_bout, semirestador_1_bout;

  SemiRestador semirestador_1 (.A(A[0]), .B(B[0]), .D(D[0]), .Bout(semirestador_1_bout));
  RestadorCompleto restadorcompleto_1 (
    .Bin(semirestador_1_bout), .A(A[1]), .B(B[1]), .D(D[1]), .Bout(restadorcompleto_1_bout));
  RestadorCompleto restadorcompleto_2 (
    .Bin(restadorcompleto_1_bout), .A(A[2]), .B(B[2]), .D(D[2]), .Bout(restadorcompleto_2_bout));
  RestadorCompleto restadorcompleto_3 (.Bin(restadorcompleto_2_bout), .A(A[3]), .B(B[3]), .D(D[3]), .Bout(Borrow));
endmodule

module SemiRestador (
  input  A,
  input  B,
  output D,
  output Bout
);

  xor xor_1 (D, B, A);
  and and_1 (Bout, ~A, B);  // AND_Gate
endmodule

module RestadorCompleto (
  input  Bin,
  input  A,
  input  B,
  output D,
  output Bout
);

  wire and_1_out, and_2_out, and_3_out, or_1_out, xor_1_out;

  xor xor_1 (xor_1_out, B, A);
  and and_1 (and_1_out, ~A, B);  // AND_Gate
  and and_2 (and_2_out, ~A, Bin);  // AND_Gate
  and and_3 (and_3_out, B, Bin);
  xor xor_2 (D, xor_1_out, Bin);
  or or_1 (or_1_out, and_1_out, and_2_out);
  or or_2 (Bout, or_1_out, and_3_out);
endmodule

module ComplementoALaBase (
  input  [3:0] A,
  output [3:0] Cb,
  output Signo
);

  wire [3:0] sumador_1_suma, xor_1_out;

  BitSelector #(.width(4)) bitselector_1 (.in(A), .out(Signo), .sel(2'b11));
  assign xor_1_out = A ^ 4'b1111;  // XOR_Gate xor_1, 4 bits wide
  Sumador sumador_1 (.A(xor_1_out), .B(4'b0001), .SUMA(sumador_1_suma));  // open: CARRY
  Multiplexer #(.width(4)) multiplexer_1 (.in0(A), .in1(sumador_1_suma), .out(Cb), .sel(Signo));
endmodule

module SemiSumador (
  input  A,
  input  B,
  output S,
  output C
);

  xor xor_1 (S, B, A);
  and and_1 (C, B, A);
endmodule

module SumadorCompleto (
  input  Cin,
  input  A,
  input  B,
  output S,
  output Cout
);

  wire and_1_out, and_2_out, and_3_out, xor_1_out;

  xor xor_1 (xor_1_out, B, A);
  and and_1 (and_1_out, B, A);
  and and_2 (and_2_out, B, Cin);
  and and_3 (and_3_out, A, Cin);
  xor xor_2 (S, xor_1_out, Cin);
  or or_1 (Cout, and_1_out, and_2_out, and_3_out);
endmodule

module DesplazaDerecha (
  input  [1:0] Cantidad,
  input  [3:0] Dato,
  output [3:0] Salida
);

  Multiplexer #(.select(2), .width(4)) multiplexer_1 (
    .in0(Dato), .in1({1'b0, Dato[3:1]}), .in2({2'b00, Dato[3:2]}), .in3({3'b000, Dato[3]}), .out(Salida),
    .sel(Cantidad));
endmodule

module DesplazaDerechaAritmetico (
  input  [1:0] Cantidad,
  input  [3:0] Dato,
  output [3:0] Salida
);

  Multiplexer #(.select(2), .width(4)) multiplexer_1 (
    .in0(Dato), .in1({{2{Dato[3]}}, Dato[2:1]}), .in2({{3{Dato[3]}}, Dato[2]}), .in3({4{Dato[3]}}),
    .out(Salida), .sel(Cantidad));
endmodule

module DesplazaIzquierda (
  input  [1:0] Cantidad,
  input  [3:0] Dato,
  output [3:0] Salida
);

  Multiplexer #(.select(2), .width(4)) multiplexer_1 (
    .in0(Dato), .in1({Dato[2:0], 1'b0}), .in2({Dato[1:0], 2'b00}), .in3({Dato[0], 3'b000}), .out(Salida),
    .sel(Cantidad));
endmodule

module ComparadorCompleto (
  input  [3:0] A,
  input  [3:0] B,
  output out_3,
  output out_4,
  output out_5,
  output out_6,
  output out_7,
  output out_8
);

  wire bitselector_1_out, overflow_1_oflw, overflow_2_oflw, signo_1_a3, signo_1_b3, signo_1_d3;
  wire [3:0] restador_1_d, restador_2_d;

  Restador restador_1 (.A(A), .B(B), .D(restador_1_d));  // open: Borrow
  Restador restador_2 (.A(B), .B(A), .D(restador_2_d));  // open: Borrow
  Signo signo_1 (.A(A), .B(B), .D(restador_1_d), .D3(signo_1_d3), .B3(signo_1_b3), .A3(signo_1_a3));
  BitSelector #(.width(4)) bitselector_1 (.in(restador_2_d), .out(bitselector_1_out), .sel(2'b11));
  nor nor_1 (out_3, restador_1_d[0], restador_1_d[1], restador_1_d[2], restador_1_d[3]);
  not not_1 (out_4, out_3);
  Overflow overflow_1 (.A3(signo_1_a3), .B3(signo_1_b3), .D3(signo_1_d3), .Oflw(overflow_1_oflw));
  Overflow overflow_2 (.A3(signo_1_b3), .B3(signo_1_a3), .D3(bitselector_1_out), .Oflw(overflow_2_oflw));
  xor xor_1 (out_5, signo_1_d3, overflow_1_oflw);
  xor xor_2 (out_7, bitselector_1_out, overflow_2_oflw);
  not not_2 (out_6, out_5);
  not not_3 (out_8, out_7);
endmodule

module Overflow (
  input  A3,
  input  B3,
  input  D3,
  output Oflw
);

  wire and_1_out, and_2_out;

  and and_1 (and_1_out, ~A3, D3, B3);  // AND_Gate
  and and_2 (and_2_out, A3, ~D3, ~B3);  // AND_Gate
  or or_1 (Oflw, and_1_out, and_2_out);
endmodule

module Signo (
  input  [3:0] A,
  input  [3:0] B,
  input  [3:0] D,
  output D3,
  output B3,
  output A3
);

  BitSelector #(.width(4)) bitselector_1 (.in(D), .out(D3), .sel(2'b11));
  BitSelector #(.width(4)) bitselector_2 (.in(B), .out(B3), .sel(2'b11));
  BitSelector #(.width(4)) bitselector_3 (.in(A), .out(A3), .sel(2'b11));
endmodule
