// Logisim project Comparador_D15.circ as structural Verilog
module ComparadorCompleto (
  input  [3:0] A,
  input  [3:0] B,
  output out_3,
  output out_4,
  output out_5,
  output out_6,
  output out_7,
  output out_8
);

  wire bitselector_1_out, overflow_1_oflw, overflow_2_oflw, signo_1_a3, signo_1_b3, signo_1_d3;
  wire [3:0] restador_1_d, restador_2_d;

  Restador restador_1 (.A(A), .B(B), .D(restador_1_d));  // open: Borrow
  Restador restador_2 (.A(B), .B(A), .D(restador_2_d));  // open: Borrow
  Signo signo_1 (.A(A), .B(B), .D(restador_1_d), .D3(signo_1_d3), .B3(signo_1_b3), .A3(signo_1_a3));
  BitSelector #(.width(4)) bitselector_1 (.in(restador_2_d), .out(bitselector_1_out), .sel(2'b11));
  nor nor_1 (out_3, restador_1_d[0], restador_1_d[1], restador_1_d[2], restador_1_d[3]);
  not not_1 (out_4, out_3);
  Overflow overflow_1 (.A3(signo_1_a3), .B3(signo_1_b3), .D3(signo_1_d3), .Oflw(overflow_1_oflw));
  Overflow overflow_2 (.A3(signo_1_b3), .B3(signo_1_a3), .D3(bitselector_1_out), .Oflw(overflow_2_oflw));
  xor xor_1 (out_5, signo_1_d3, overflow_1_oflw);
  xor xor_2 (out_7, bitselector_1_out, overflow_2_oflw);
  not not_2 (out_6, out_5);
  not not_3 (out_8, out_7);
endmodule

module SemiRestador (
  input  A,
  input  B,
  output D,
  output Bout
);

  xor xor_1 (D, B, A);
  and and_1 (Bout, ~A, B);  // AND_Gate
endmodule

module RestadorCompleto (
  input  Bin,
  input  A,
  input  B,
  output D,
  output Bout
);

  wire and_1_out, and_2_out, and_3_out, or_1_out, xor_1_out;

  xor xor_1 (xor_1_out, B, A);
  and and_1 (and_1_out, ~A, B);  // AND_Gate
  and and_2 (and_2_out, ~A, Bin);  // AND_Gate
  and and_3 (and_3_out, B, Bin);
  xor xor_2 (D, xor_1_out, Bin);
  or or_1 (or_1_out, and_1_out, and_2_out);
  or or_2 (Bout, or_1_out, and_3_out);
endmodule

module Restador (
  input  [3:0] A,
  input  [3:0] B,
  output [3:0] D,
  output Borrow
);

  wire restadorcompleto_1_bout, restadorcompleto_2_bout, semirestador_1_bout;

  SemiRestador semirestador_1 (.A(A[0]), .B(B[0]), .D(D[0]), .Bout(semirestador_1_bout));
  RestadorCompleto restadorcompleto_1 (
    .Bin(semirestador_1_bout), .A(A[1]), .B(B[1]), .D(D[1]), .Bout(restadorcompleto_1_bout));
  RestadorCompleto restadorcompleto_2 (
    .Bin(restadorcompleto_1_bout), .A(A[2]), .B(B[2]), .D(D[2]), .Bout(restadorcompleto_2_bout));
  RestadorCompleto restadorcompleto_3 (.Bin(restadorcompleto_2_bout), .A(A[3]), .B(B[3]), .D(D[3]), .Bout(Borrow));
endmodule

module Overflow (
  input  A3,
  input  B3,
  input  D3,
  output Oflw
);

  wire and_1_out, and_2_out;

  and and_1 (and_1_out, ~A3, D3, B3);  // AND_Gate
  and and_2 (and_2_out, A3, ~D3, ~B3);  // AND_Gate
  or or_1 (Oflw, and_1_out, and_2_out);
endmodule

module Signo (
  input  [3:0] A,
  input  [3:0] B,
  input  [3:0] D,
  output D3,
  output B3,
  output A3
);

  BitSelector #(.width(4)) bitselector_1 (.in(D), .out(D3), .sel(2'b11));
  BitSelector #(.width(4)) bitselector_2 (.in(B), .out(B3), .sel(2'b11));
  BitSelector #(.width(4)) bitselector_3 (.in(A), .out(A3), .sel(2'b11));
endmodule
