// Logisim project D_12.circ as structural Verilog: 8 circuits, main circuit main
module main (
  input  [3:0] A,
  input  [3:0] B,
  output [3:0] out_3
);

  wire complementoalabase_1_signo, restador_1_borrowout;
  wire [3:0] complementoalabase_1_cb;

  Hex_Digit_Display hex_digit_display_1 (.value(A));  // open: dp
  Hex_Digit_Display hex_digit_display_2 (.value(B));  // open: dp
  Restador restador_1 (.A(A), .B(B), .Resta(out_3), .BorrowOut(restador_1_borrowout));
  LED led_1 (.in(restador_1_borrowout));
  Hex_Digit_Display hex_digit_display_3 (.value(out_3));  // open: dp
  _7_Segment_Display u_7_segment_display_1 (.g(complementoalabase_1_signo));  // open: f, a, b, e, d, c, dp
  ComplementoALaBase complementoalabase_1 (.A(out_3), .Cb(complementoalabase_1_cb), .Signo(complementoalabase_1_signo));
  Hex_Digit_Display hex_digit_display_4 (.value(complementoalabase_1_cb));  // open: dp
endmodule

module Restador (
  input  [3:0] A,
  input  [3:0] B,
  output [3:0] Resta,
  output BorrowOut
);

  wire restadorcompleto_1_bout, restadorcompleto_2_bout, semirestador_1_borrowout;

  SemiRestador semirestador_1 (.A(A[0]), .B(B[0]), .Resta(Resta[0]), .BorrowOut(semirestador_1_borrowout));
  RestadorCompleto restadorcompleto_1 (
    .Bin(semirestador_1_borrowout), .A(A[1]), .B(B[1]), .Resta(Resta[1]), .Bout(restadorcompleto_1_bout));
  RestadorCompleto restadorcompleto_2 (
    .Bin(restadorcompleto_1_bout), .A(A[2]), .B(B[2]), .Resta(Resta[2]), .Bout(restadorcompleto_2_bout));
  RestadorCompleto restadorcompleto_3 (
    .Bin(restadorcompleto_2_bout), .A(A[3]), .B(B[3]), .Resta(Resta[3]), .Bout(BorrowOut));
endmodule

module SemiRestador (
  input  A,
  input  B,
  output Resta,
  output BorrowOut
);

  xor xor_1 (Resta, B, A);
  and and_1 (BorrowOut, ~A, B);  // AND_Gate
endmodule

module RestadorCompleto (
  input  Bin,
  input  A,
  input  B,
  output Resta,
  output Bout
);

  wire and_1_out, and_2_out, and_3_out, or_1_out, xor_1_out;

  xor xor_1 (xor_1_out, B, A);
  and and_1 (and_1_out, ~A, Bin);  // AND_Gate
  and and_2 (and_2_out, ~A, B);  // AND_Gate
  and and_3 (and_3_out, B, Bin);
  xor xor_2 (Resta, xor_1_out, Bin);
  or or_1 (or_1_out, and_1_out, and_2_out);
  or or_2 (Bout, or_1_out, and_3_out);
endmodule

module ComplementoALaBase (
  input  [3:0] A,
  output [3:0] Cb,
  output Signo
);

  wire [3:0] sumador_1_sum, xor_1_out;

  BitSelector #(.width(4)) bitselector_1 (.in(A), .out(Signo), .sel(2'b11));
  assign xor_1_out = A ^ 4'b1111;  // XOR_Gate xor_1, 4 bits wide
  Sumador sumador_1 (.A(xor_1_out), .B(4'b0001), .Sum(sumador_1_sum));  // open: Carry
  Multiplexer #(.width(4)) multiplexer_1 (.in0(A), .in1(sumador_1_sum), .out(Cb), .sel(Signo));
endmodule

module SemiSumador (
  input  A,
  input  B,
  output S,
  output C
);

  xor xor_1 (S, B, A);
  and and_1 (C, B, A);
endmodule

module SumadorCompleto (
  input  Cin,
  input  A,
  input  B,
  output S,
  output Cout
);

  wire and_1_out, and_2_out, and_3_out, xor_1_out;

  xor xor_1 (xor_1_out, B, A);
  and and_1 (and_1_out, B, A);
  and and_2 (and_2_out, B, Cin);
  and and_3 (and_3_out, A, Cin);
  xor xor_2 (S, xor_1_out, Cin);
  or or_1 (Cout, and_1_out, and_2_out, and_3_out);
endmodule

module Sumador (
  input  [3:0] A,
  input  [3:0] B,
  output [3:0] Sum,
  output Carry
);

  wire semisumador_1_c, sumadorcompleto_1_cout, sumadorcompleto_2_cout;

  SemiSumador semisumador_1 (.A(A[0]), .B(B[0]), .S(Sum[0]), .C(semisumador_1_c));
  SumadorCompleto sumadorcompleto_1 (
    .Cin(semisumador_1_c), .A(A[1]), .B(B[1]), .S(Sum[1]), .Cout(sumadorcompleto_1_cout));
  SumadorCompleto sumadorcompleto_2 (
    .Cin(sumadorcompleto_1_cout), .A(A[2]), .B(B[2]), .S(Sum[2]), .Cout(sumadorcompleto_2_cout));
  SumadorCompleto sumadorcompleto_3 (.Cin(sumadorcompleto_2_cout), .A(A[3]), .B(B[3]), .S(Sum[3]), .Cout(Carry));
endmodule
