// Logisim project Desplazador_D18.circ as structural Verilog: 4 circuits, main circuit main
module main (
  input  [1:0] in_1,
  input  [3:0] in_2,
  output [3:0] out_3
);

  DesplazaDerecha desplazaderecha_1 (.Cantidad(in_1), .Dato(in_2), .Salida(out_3));
endmodule

module DesplazaDerecha (
  input  [1:0] Cantidad,
  input  [3:0] Dato,
  output [3:0] Salida
);

  Multiplexer #(.select(2), .width(4)) multiplexer_1 (
    .in0(Dato), .in1({1'b0, Dato[3:1]}), .in2({2'b00, Dato[3:2]}), .in3({3'b000, Dato[3]}), .out(Salida),
    .sel(Cantidad));
endmodule

module DesplazaDerechaAritmetico (
  input  [1:0] Cantidad,
  input  [3:0] Dato,
  output [3:0] Salida
);

  Multiplexer #(.select(2), .width(4)) multiplexer_1 (
    .in0(Dato), .in1({{2{Dato[3]}}, Dato[2:1]}), .in2({{3{Dato[3]}}, Dato[2]}), .in3({4{Dato[3]}}),
    .out(Salida), .sel(Cantidad));
endmodule

module DesplazaIzquierda (
  input  [1:0] Cantidad,
  input  [3:0] Dato,
  output [3:0] Salida
);

  Multiplexer #(.select(2), .width(4)) multiplexer_1 (
    .in0(Dato), .in1({Dato[2:0], 1'b0}), .in2({Dato[1:0], 2'b00}), .in3({Dato[0], 3'b000}), .out(Salida),
    .sel(Cantidad));
endmodule
