// Logisim project Encoder7Seg.circ as structural Verilog: 10 circuits, main circuit main
module main (
  input  A,
  input  B,
  input  C,
  input  D,
  output SA,
  output SB,
  output SC,
  output SD,
  output SE,
  output SF,
  output SG
);

  FA fa_1 (.A(A), .B(B), .C(C), .D(D), .F1(SA));
  FB fb_1 (.D(D), .C(C), .B(B), .A(A), .F2(SB));
  FC fc_1 (.D(D), .C(C), .B(B), .A(A), .F3(SC));
  FD fd_1 (.D(D), .C(C), .B(B), .A(A), .F4(SD));
  FE fe_1 (.D(D), .C(C), .B(B), .A(A), .F5(SE));
  FF ff_1 (.D(D), .C(C), .B(B), .A(A), .F6(SF));
  FG fg_1 (.D(D), .C(C), .B(B), .A(A), .F7(SG));
endmodule

module FA (
  input  A,
  input  B,
  input  C,
  input  D,
  output F1
);

  wire nand_1_out, nand_2_out, nand_3_out, nand_4_out, nand_5_out, nand_6_out, nand_7_out, nand_8_out,
       nand_9_out, nand_10_out, nand_11_out, nand_12_out, nand_13_out, nand_14_out, nand_15_out, nand_16_out,
       nand_17_out, nand_18_out, nand_19_out, nand_20_out, nand_21_out, nand_22_out, nand_23_out,
       nand_24_out, nand_25_out, nand_26_out, nand_27_out, nand_28_out, nand_29_out, nand_30_out,
       nand_31_out, nand_32_out, nand_33_out, nand_34_out;

  nand nand_1 (nand_1_out, A, A);
  nand nand_2 (nand_2_out, B, B);
  nand nand_3 (nand_3_out, C, C);
  nand nand_4 (nand_4_out, D, D);
  nand nand_5 (nand_5_out, nand_2_out, nand_4_out);
  nand nand_6 (nand_6_out, B, C);
  nand nand_7 (nand_7_out, A, nand_4_out);
  nand nand_8 (nand_8_out, nand_1_out, C);
  nand nand_9 (nand_9_out, nand_2_out, nand_3_out);
  nand nand_10 (nand_10_out, B, D);
  nand nand_11 (nand_11_out, nand_5_out, nand_5_out);
  nand nand_12 (nand_12_out, nand_6_out, nand_6_out);
  nand nand_13 (nand_13_out, nand_7_out, nand_7_out);
  nand nand_14 (nand_14_out, nand_8_out, nand_8_out);
  nand nand_15 (nand_15_out, nand_9_out, nand_9_out);
  nand nand_16 (nand_16_out, nand_10_out, nand_10_out);
  nand nand_17 (nand_17_out, A, nand_15_out);
  nand nand_18 (nand_18_out, nand_1_out, nand_16_out);
  nand nand_19 (nand_19_out, nand_11_out, nand_11_out);
  nand nand_20 (nand_20_out, nand_12_out, nand_12_out);
  nand nand_21 (nand_21_out, nand_13_out, nand_13_out);
  nand nand_22 (nand_22_out, nand_14_out, nand_14_out);
  nand nand_23 (nand_23_out, nand_17_out, nand_17_out);
  nand nand_24 (nand_24_out, nand_18_out, nand_18_out);
  nand nand_25 (nand_25_out, nand_19_out, nand_20_out);
  nand nand_26 (nand_26_out, nand_21_out, nand_22_out);
  nand nand_27 (nand_27_out, nand_23_out, nand_23_out);
  nand nand_28 (nand_28_out, nand_24_out, nand_24_out);
  nand nand_29 (nand_29_out, nand_25_out, nand_25_out);
  nand nand_30 (nand_30_out, nand_26_out, nand_26_out);
  nand nand_31 (nand_31_out, nand_27_out, nand_28_out);
  nand nand_32 (nand_32_out, nand_29_out, nand_30_out);
  nand nand_33 (nand_33_out, nand_32_out, nand_32_out);
  nand nand_34 (nand_34_out, nand_31_out, nand_31_out);
  nand nand_35 (F1, nand_33_out, nand_34_out);
endmodule

module FB (
  input  D,
  input  C,
  input  B,
  input  A,
  output F2
);

  wire nand_1_out, nand_2_out, nand_3_out, nand_4_out, nand_5_out, nand_6_out, nand_7_out, nand_8_out,
       nand_9_out, nand_10_out, nand_11_out, nand_12_out, nand_13_out, nand_14_out, nand_15_out, nand_16_out,
       nand_17_out, nand_18_out, nand_19_out, nand_20_out, nand_21_out, nand_22_out, nand_23_out,
       nand_24_out, nand_25_out, nand_26_out, nand_27_out, nand_28_out, nand_29_out, nand_30_out, nand_31_out;

  nand nand_1 (nand_1_out, A, A);
  nand nand_2 (nand_2_out, B, B);
  nand nand_3 (nand_3_out, C, C);
  nand nand_4 (nand_4_out, D, D);
  nand nand_5 (nand_5_out, nand_2_out, nand_4_out);
  nand nand_6 (nand_6_out, nand_2_out, nand_3_out);
  nand nand_7 (nand_7_out, nand_3_out, D);
  nand nand_8 (nand_8_out, nand_3_out, nand_4_out);
  nand nand_9 (nand_9_out, C, D);
  nand nand_10 (nand_10_out, nand_5_out, nand_5_out);
  nand nand_11 (nand_11_out, nand_6_out, nand_6_out);
  nand nand_12 (nand_12_out, nand_7_out, nand_7_out);
  nand nand_13 (nand_13_out, nand_8_out, nand_8_out);
  nand nand_14 (nand_14_out, nand_9_out, nand_9_out);
  nand nand_15 (nand_15_out, nand_1_out, nand_14_out);
  nand nand_16 (nand_16_out, nand_10_out, nand_10_out);
  nand nand_17 (nand_17_out, nand_11_out, nand_11_out);
  nand nand_18 (nand_18_out, A, nand_12_out);
  nand nand_19 (nand_19_out, nand_1_out, nand_13_out);
  nand nand_20 (nand_20_out, nand_16_out, nand_17_out);
  nand nand_21 (nand_21_out, nand_18_out, nand_18_out);
  nand nand_22 (nand_22_out, nand_19_out, nand_19_out);
  nand nand_23 (nand_23_out, nand_15_out, nand_15_out);
  nand nand_24 (nand_24_out, nand_21_out, nand_21_out);
  nand nand_25 (nand_25_out, nand_22_out, nand_22_out);
  nand nand_26 (nand_26_out, nand_23_out, nand_23_out);
  nand nand_27 (nand_27_out, nand_24_out, nand_25_out);
  nand nand_28 (nand_28_out, nand_20_out, nand_20_out);
  nand nand_29 (nand_29_out, nand_27_out, nand_27_out);
  nand nand_30 (nand_30_out, nand_28_out, nand_29_out);
  nand nand_31 (nand_31_out, nand_30_out, nand_30_out);
  nand nand_32 (F2, nand_31_out, nand_26_out);
endmodule

module FC (
  input  D,
  input  C,
  input  B,
  input  A,
  output F3
);

  wire nand_1_out, nand_2_out, nand_3_out, nand_4_out, nand_5_out, nand_6_out, nand_7_out, nand_8_out,
       nand_9_out, nand_10_out, nand_11_out, nand_12_out, nand_13_out, nand_14_out, nand_15_out, nand_16_out,
       nand_17_out, nand_18_out, nand_19_out, nand_20_out, nand_21_out, nand_22_out, nand_23_out, nand_24_out;

  nand nand_1 (nand_1_out, A, A);
  nand nand_2 (nand_2_out, B, B);
  nand nand_3 (nand_3_out, C, C);
  nand nand_4 (nand_4_out, nand_2_out, nand_3_out);
  nand nand_5 (nand_5_out, nand_1_out, D);
  nand nand_6 (nand_6_out, nand_1_out, B);
  nand nand_7 (nand_7_out, A, nand_2_out);
  nand nand_8 (nand_8_out, nand_3_out, D);
  nand nand_9 (nand_9_out, nand_4_out, nand_4_out);
  nand nand_10 (nand_10_out, nand_5_out, nand_5_out);
  nand nand_11 (nand_11_out, nand_6_out, nand_6_out);
  nand nand_12 (nand_12_out, nand_7_out, nand_7_out);
  nand nand_13 (nand_13_out, nand_8_out, nand_8_out);
  nand nand_14 (nand_14_out, nand_9_out, nand_9_out);
  nand nand_15 (nand_15_out, nand_10_out, nand_10_out);
  nand nand_16 (nand_16_out, nand_11_out, nand_11_out);
  nand nand_17 (nand_17_out, nand_12_out, nand_12_out);
  nand nand_18 (nand_18_out, nand_13_out, nand_13_out);
  nand nand_19 (nand_19_out, nand_14_out, nand_15_out);
  nand nand_20 (nand_20_out, nand_16_out, nand_17_out);
  nand nand_21 (nand_21_out, nand_19_out, nand_19_out);
  nand nand_22 (nand_22_out, nand_20_out, nand_20_out);
  nand nand_23 (nand_23_out, nand_21_out, nand_22_out);
  nand nand_24 (nand_24_out, nand_23_out, nand_23_out);
  nand nand_25 (F3, nand_24_out, nand_18_out);
endmodule

module FD (
  input  D,
  input  C,
  input  B,
  input  A,
  output F4
);

  wire nand_1_out, nand_2_out, nand_3_out, nand_4_out, nand_5_out, nand_6_out, nand_7_out, nand_8_out,
       nand_9_out, nand_10_out, nand_11_out, nand_12_out, nand_13_out, nand_14_out, nand_15_out, nand_16_out,
       nand_17_out, nand_18_out, nand_19_out, nand_20_out, nand_21_out, nand_22_out, nand_23_out,
       nand_24_out, nand_25_out, nand_26_out, nand_27_out, nand_28_out, nand_29_out, nand_30_out,
       nand_31_out, nand_32_out, nand_33_out, nand_34_out, nand_35_out, nand_36_out, nand_37_out,
       nand_38_out, nand_39_out, nand_40_out, nand_41_out, nand_42_out;

  nand nand_1 (nand_1_out, D, D);
  nand nand_2 (nand_2_out, C, C);
  nand nand_3 (nand_3_out, B, B);
  nand nand_4 (nand_4_out, A, A);
  nand nand_5 (nand_5_out, nand_3_out, C);
  nand nand_6 (nand_6_out, C, nand_1_out);
  nand nand_7 (nand_7_out, nand_2_out, nand_1_out);
  nand nand_8 (nand_8_out, B, nand_1_out);
  nand nand_9 (nand_9_out, nand_2_out, D);
  nand nand_10 (nand_10_out, nand_3_out, D);
  nand nand_11 (nand_11_out, nand_7_out, nand_7_out);
  nand nand_12 (nand_12_out, nand_8_out, nand_8_out);
  nand nand_13 (nand_13_out, nand_9_out, nand_9_out);
  nand nand_14 (nand_14_out, nand_10_out, nand_10_out);
  nand nand_15 (nand_15_out, nand_5_out, nand_5_out);
  nand nand_16 (nand_16_out, nand_6_out, nand_6_out);
  nand nand_17 (nand_17_out, nand_3_out, nand_11_out);
  nand nand_18 (nand_18_out, A, nand_12_out);
  nand nand_19 (nand_19_out, B, nand_13_out);
  nand nand_20 (nand_20_out, A, nand_14_out);
  nand nand_21 (nand_21_out, nand_4_out, nand_15_out);
  nand nand_22 (nand_22_out, nand_4_out, nand_16_out);
  nand nand_23 (nand_23_out, nand_17_out, nand_17_out);
  nand nand_24 (nand_24_out, nand_18_out, nand_18_out);
  nand nand_25 (nand_25_out, nand_19_out, nand_19_out);
  nand nand_26 (nand_26_out, nand_20_out, nand_20_out);
  nand nand_27 (nand_27_out, nand_21_out, nand_21_out);
  nand nand_28 (nand_28_out, nand_22_out, nand_22_out);
  nand nand_29 (nand_29_out, nand_23_out, nand_23_out);
  nand nand_30 (nand_30_out, nand_24_out, nand_24_out);
  nand nand_31 (nand_31_out, nand_25_out, nand_25_out);
  nand nand_32 (nand_32_out, nand_26_out, nand_26_out);
  nand nand_33 (nand_33_out, nand_27_out, nand_27_out);
  nand nand_34 (nand_34_out, nand_28_out, nand_28_out);
  nand nand_35 (nand_35_out, nand_29_out, nand_30_out);
  nand nand_36 (nand_36_out, nand_31_out, nand_32_out);
  nand nand_37 (nand_37_out, nand_33_out, nand_34_out);
  nand nand_38 (nand_38_out, nand_35_out, nand_35_out);
  nand nand_39 (nand_39_out, nand_36_out, nand_36_out);
  nand nand_40 (nand_40_out, nand_37_out, nand_37_out);
  nand nand_41 (nand_41_out, nand_38_out, nand_39_out);
  nand nand_42 (nand_42_out, nand_41_out, nand_41_out);
  nand nand_43 (F4, nand_42_out, nand_40_out);
endmodule

module FE (
  input  D,
  input  C,
  input  B,
  input  A,
  output F5
);

  Multiplexer #(.select(4)) multiplexer_1 (
    .in0(1'b1), .in1(1'b0), .in2(1'b1), .in3(1'b0), .in4(1'b0), .in5(1'b0), .in6(1'b1), .in7(1'b0),
    .in8(1'b1), .in9(1'b0), .in10(1'b1), .in11(1'b1), .in12(1'b1), .in13(1'b1), .in14(1'b1), .in15(1'b1),
    .out(F5), .sel({A, B, C, D}));
endmodule

module FF (
  input  D,
  input  C,
  input  B,
  input  A,
  output F6
);

  wire nor_1_out, nor_2_out, nor_3_out, nor_4_out, nor_5_out, nor_6_out, nor_7_out, nor_8_out, nor_9_out,
       nor_10_out, nor_11_out, nor_12_out, nor_13_out, nor_14_out, nor_15_out, nor_16_out, nor_17_out,
       nor_18_out, nor_19_out, nor_20_out, nor_21_out, nor_22_out;

  nor nor_1 (nor_1_out, D, D);
  nor nor_2 (nor_2_out, C, C);
  nor nor_3 (nor_3_out, B, B);
  nor nor_4 (nor_4_out, A, A);
  nor nor_5 (nor_5_out, B, nor_1_out);
  nor nor_6 (nor_6_out, B, nor_2_out);
  nor nor_7 (nor_7_out, nor_2_out, nor_1_out);
  nor nor_8 (nor_8_out, nor_4_out, nor_3_out);
  nor nor_9 (nor_9_out, C, nor_1_out);
  nor nor_10 (nor_10_out, nor_5_out, nor_5_out);
  nor nor_11 (nor_11_out, nor_6_out, nor_6_out);
  nor nor_12 (nor_12_out, nor_7_out, nor_7_out);
  nor nor_13 (nor_13_out, nor_8_out, nor_8_out);
  nor nor_14 (nor_14_out, nor_9_out, nor_9_out);
  nor nor_15 (nor_15_out, A, nor_10_out);
  nor nor_16 (nor_16_out, A, nor_11_out);
  nor nor_17 (nor_17_out, A, nor_12_out);
  nor nor_18 (nor_18_out, nor_13_out, nor_14_out);
  nor nor_19 (nor_19_out, nor_15_out, nor_16_out);
  nor nor_20 (nor_20_out, nor_17_out, nor_18_out);
  nor nor_21 (nor_21_out, nor_19_out, nor_19_out);
  nor nor_22 (nor_22_out, nor_20_out, nor_20_out);
  nor nor_23 (F6, nor_21_out, nor_22_out);
endmodule

module FG (
  input  D,
  input  C,
  input  B,
  input  A,
  output F7
);

  wire nor_1_out, nor_2_out, nor_3_out, nor_4_out, nor_5_out, nor_6_out, nor_7_out, nor_8_out, nor_9_out,
       nor_10_out, nor_11_out, nor_12_out, nor_13_out, nor_14_out, nor_15_out, nor_16_out, nor_17_out,
       nor_18_out, nor_19_out, nor_20_out, nor_21_out, nor_22_out, nor_23_out, nor_24_out, nor_25_out;

  nor nor_1 (nor_1_out, D, D);
  nor nor_2 (nor_2_out, C, C);
  nor nor_3 (nor_3_out, B, B);
  nor nor_4 (nor_4_out, A, A);
  nor nor_5 (nor_5_out, B, C);
  nor nor_6 (nor_6_out, A, nor_3_out);
  nor nor_7 (nor_7_out, nor_2_out, nor_1_out);
  nor nor_8 (nor_8_out, nor_4_out, nor_3_out);
  nor nor_9 (nor_9_out, C, D);
  nor nor_10 (nor_10_out, nor_5_out, nor_5_out);
  nor nor_11 (nor_11_out, nor_6_out, nor_6_out);
  nor nor_12 (nor_12_out, nor_7_out, nor_7_out);
  nor nor_13 (nor_13_out, nor_8_out, nor_8_out);
  nor nor_14 (nor_14_out, nor_9_out, nor_9_out);
  nor nor_15 (nor_15_out, A, nor_10_out);
  nor nor_16 (nor_16_out, nor_11_out, nor_12_out);
  nor nor_17 (nor_17_out, nor_13_out, nor_14_out);
  nor nor_18 (nor_18_out, nor_15_out, nor_15_out);
  nor nor_19 (nor_19_out, nor_16_out, nor_16_out);
  nor nor_20 (nor_20_out, nor_17_out, nor_17_out);
  nor nor_21 (nor_21_out, nor_18_out, nor_18_out);
  nor nor_22 (nor_22_out, nor_19_out, nor_19_out);
  nor nor_23 (nor_23_out, nor_20_out, nor_20_out);
  nor nor_24 (nor_24_out, nor_21_out, nor_22_out);
  nor nor_25 (nor_25_out, nor_24_out, nor_24_out);
  nor nor_26 (F7, nor_25_out, nor_23_out);
endmodule

module punto8 (
  input  E15,
  input  E14,
  input  E13,
  input  E12,
  input  E11,
  input  E10,
  input  E9,
  input  E8,
  input  E7,
  input  E6,
  input  E5,
  input  E4,
  input  E3,
  input  E2,
  input  E1
);

  wire encodersimple_1_a, encodersimple_1_b, encodersimple_1_c, encodersimple_1_d, main_1_sa, main_1_sb,
       main_1_sc, main_1_sd, main_1_se, main_1_sf, main_1_sg;

  EncoderSimple encodersimple_1 (
    .E15(E15), .E14(E14), .E13(E13), .E12(E12), .E11(E11), .E10(E10), .E9(E9), .E8(E8), .E7(E7), .E6(E6),
    .E5(E5), .E4(E4), .E3(E3), .E2(E2), .E1(E1), .A(encodersimple_1_a), .B(encodersimple_1_b),
    .C(encodersimple_1_c), .D(encodersimple_1_d));
  main main_1 (
    .A(encodersimple_1_a), .B(encodersimple_1_b), .C(encodersimple_1_c), .D(encodersimple_1_d),
    .SA(main_1_sa), .SB(main_1_sb), .SC(main_1_sc), .SD(main_1_sd), .SE(main_1_se), .SF(main_1_sf),
    .SG(main_1_sg));
  _7_Segment_Display u_7_segment_display_1 (
    .g(main_1_sg), .f(main_1_sf), .a(main_1_sa), .b(main_1_sb), .e(main_1_se), .d(main_1_sd), .c(main_1_sc));  // open: dp
endmodule

module EncoderSimple (
  input  E15,
  input  E14,
  input  E13,
  input  E12,
  input  E11,
  input  E10,
  input  E9,
  input  E8,
  input  E7,
  input  E6,
  input  E5,
  input  E4,
  input  E3,
  input  E2,
  input  E1,
  output A,
  output B,
  output C,
  output D
);

  or or_1 (A, E8, E9, E10, E11, E12, E13, E14, E15);
  or or_2 (B, E4, E5, E6, E7, E12, E13, E14, E15);
  or or_3 (C, E2, E3, E6, E7, E10, E11, E14, E15);
  or or_4 (D, E1, E3, E5, E7, E9, E11, E13, E15);
endmodule
