// Logisim project SumadorBCD_embebidos.circ as structural Verilog: 6 circuits, main circuit main
module main (
  input  [3:0] A,
  input  [3:0] B,
  output [3:0] BCD0,
  output [3:0] BCD1
);

  Hex_Digit_Display hex_digit_display_1 (.value(A));  // open: dp
  Hex_Digit_Display hex_digit_display_2 (.value(B));  // open: dp
  SumadorBCD sumadorbcd_1 (.A(A), .B(B), .BCD0(BCD0), .BCD1(BCD1));
  Hex_Digit_Display hex_digit_display_3 (.value(BCD1));  // open: dp
  Hex_Digit_Display hex_digit_display_4 (.value(BCD0));  // open: dp
endmodule

module SumadorBCD (
  input  [3:0] A,
  input  [3:0] B,
  output [3:0] BCD0,
  output [3:0] BCD1
);

  wire or_1_out, rango_1_outofrange, semisumador_1_carry, sumador_1_carry, sumadorcompleto_1_cout,
       sumadorcompleto_2_cout, sumadorcompleto_3_cout;
  wire [3:0] semisumador_1_sum, sumador_1_sum;

  SemiSumador semisumador_1 (.A(A[0]), .B(B[0]), .Sum(semisumador_1_sum[0]), .Carry(semisumador_1_carry));
  SumadorCompleto sumadorcompleto_1 (
    .Cin(semisumador_1_carry), .A(A[1]), .B(B[1]), .Sum(semisumador_1_sum[1]), .Cout(sumadorcompleto_1_cout));
  SumadorCompleto sumadorcompleto_2 (
    .Cin(sumadorcompleto_1_cout), .A(A[2]), .B(B[2]), .Sum(semisumador_1_sum[2]),
    .Cout(sumadorcompleto_2_cout));
  SumadorCompleto sumadorcompleto_3 (
    .Cin(sumadorcompleto_2_cout), .A(A[3]), .B(B[3]), .Sum(semisumador_1_sum[3]),
    .Cout(sumadorcompleto_3_cout));
  Rango rango_1 (.A(semisumador_1_sum), .OutOfRange(rango_1_outofrange));
  Sumador sumador_1 (.A(semisumador_1_sum), .B(4'b0110), .Sum(sumador_1_sum), .Carry(sumador_1_carry));
  or or_1 (or_1_out, rango_1_outofrange, sumadorcompleto_3_cout);
  Multiplexer #(.width(4)) multiplexer_1 (.in0(semisumador_1_sum), .in1(sumador_1_sum), .out(BCD0), .sel(or_1_out));
  or or_2 (BCD1[0], sumador_1_carry, sumadorcompleto_3_cout);

  assign BCD1[3:1] = 3'b000;
endmodule

module SemiSumador (
  input  A,
  input  B,
  output Sum,
  output Carry
);

  xor xor_1 (Sum, B, A);
  and and_1 (Carry, B, A);
endmodule

module SumadorCompleto (
  input  Cin,
  input  A,
  input  B,
  output Sum,
  output Cout
);

  wire and_1_out, and_2_out, and_3_out, xor_1_out;

  xor xor_1 (xor_1_out, B, A);
  and and_1 (and_1_out, B, A);
  and and_2 (and_2_out, B, Cin);
  and and_3 (and_3_out, A, Cin);
  or or_1 (Cout, and_1_out, and_2_out, and_3_out);
  xor xor_2 (Sum, xor_1_out, Cin);
endmodule

module Sumador (
  input  [3:0] A,
  input  [3:0] B,
  output [3:0] Sum,
  output Carry
);

  wire semisumador_1_carry, sumadorcompleto_1_cout, sumadorcompleto_2_cout;

  SemiSumador semisumador_1 (.A(A[0]), .B(B[0]), .Sum(Sum[0]), .Carry(semisumador_1_carry));
  SumadorCompleto sumadorcompleto_1 (
    .Cin(semisumador_1_carry), .A(A[1]), .B(B[1]), .Sum(Sum[1]), .Cout(sumadorcompleto_1_cout));
  SumadorCompleto sumadorcompleto_2 (
    .Cin(sumadorcompleto_1_cout), .A(A[2]), .B(B[2]), .Sum(Sum[2]), .Cout(sumadorcompleto_2_cout));
  SumadorCompleto sumadorcompleto_3 (.Cin(sumadorcompleto_2_cout), .A(A[3]), .B(B[3]), .Sum(Sum[3]), .Cout(Carry));
endmodule

module Rango (
  input  [3:0] A,
  output OutOfRange
);

  wire and_1_out, and_2_out;

  and and_1 (and_1_out, A[3], A[1]);
  and and_2 (and_2_out, A[3], A[2]);
  or or_1 (OutOfRange, and_1_out, and_2_out);
endmodule
