// Logisim project Sumador_embebidos.circ as structural Verilog: 4 circuits, main circuit main
module main (
  input  [3:0] A,
  input  [3:0] B,
  output [3:0] SUMA,
  output CARRY
);

  wire fulladder_1_carryout, fulladder_2_carryout, halfadder_1_carry;

  HalfAdder halfadder_1 (.B(B[0]), .A(A[0]), .Carry(halfadder_1_carry), .Sum(SUMA[0]));
  FullAdder fulladder_1 (
    .CarryIn(halfadder_1_carry), .B(B[1]), .A(A[1]), .CarryOut(fulladder_1_carryout), .Sum(SUMA[1]));
  FullAdder fulladder_2 (
    .CarryIn(fulladder_1_carryout), .B(B[2]), .A(A[2]), .CarryOut(fulladder_2_carryout), .Sum(SUMA[2]));
  FullAdder fulladder_3 (.CarryIn(fulladder_2_carryout), .B(B[3]), .A(A[3]), .CarryOut(CARRY), .Sum(SUMA[3]));
endmodule

module HalfAdder (
  input  B,
  input  A,
  output Carry,
  output Sum
);

  and and_1 (Carry, A, B);
  xor xor_1 (Sum, A, B);
endmodule

module FullAdder (
  input  CarryIn,
  input  B,
  input  A,
  output CarryOut,
  output Sum
);

  wire and_1_out, and_2_out, and_3_out, xor_1_out;

  and and_1 (and_1_out, A, B);
  and and_2 (and_2_out, A, CarryIn);
  and and_3 (and_3_out, B, CarryIn);
  xor xor_1 (xor_1_out, A, B);
  xor xor_2 (Sum, xor_1_out, CarryIn);
  or or_1 (CarryOut, and_1_out, and_2_out, and_3_out);
endmodule

module Sumador (
  input  [3:0] A,
  input  [3:0] B,
  output [3:0] Sum,
  output out_4
);

  Hex_Digit_Display hex_digit_display_1 (.value(A));  // open: dp
  Hex_Digit_Display hex_digit_display_2 (.value(B));  // open: dp
  main main_1 (.A(A), .B(B), .SUMA(Sum), .CARRY(out_4));
  Hex_Digit_Display hex_digit_display_3 (.value(Sum));  // open: dp
endmodule
