// Logisim project TP5.circ as structural Verilog: 24 circuits, main circuit TransicionJohnsonE1
module main (
);

  wire clock_1_out;
  wire [2:0] undriven, undriven_2;

  Clock clock_1 (.out(clock_1_out));
  LED led_1 (.in(undriven[0]));
  LED led_2 (.in(undriven[1]));
  LED led_3 (.in(undriven[2]));
  LED led_4 (.in(undriven_2[0]));
  LED led_5 (.in(undriven_2[1]));
  LED led_6 (.in(undriven_2[2]));
endmodule

module ContadorJohnsonE1 (
);

  wire clock_1_out, transicionjohnsone1_1_s0, transicionjohnsone1_1_s1, transicionjohnsone1_1_s2,
       transicionjohnsone1_1_s3;
  wire [3:0] counter_1_q;

  Clock clock_1 (.out(clock_1_out));
  Counter #(.max('h7), .width(4)) counter_1 (
    .Q(counter_1_q), .clk(clock_1_out));  // open: load, D, count, carry, up, clr
  TransicionJohnsonE1 transicionjohnsone1_1 (
    .C0(counter_1_q[0]), .C1(counter_1_q[1]), .C2(counter_1_q[2]), .C3(counter_1_q[3]),
    .S0(transicionjohnsone1_1_s0), .S1(transicionjohnsone1_1_s1), .S2(transicionjohnsone1_1_s2),
    .S3(transicionjohnsone1_1_s3));
  LedBar #(.matrixcols(4)) ledbar_1 (
    .led0(transicionjohnsone1_1_s3), .led1(transicionjohnsone1_1_s2), .led2(transicionjohnsone1_1_s1),
    .led3(transicionjohnsone1_1_s0));
  // Digital_Oscilloscope digital_oscilloscope_1: pin names not known; wires that end beside it: clock_1_out, transicionjohnsone1_1_s0, transicionjohnsone1_1_s1, transicionjohnsone1_1_s2, transicionjohnsone1_1_s3
endmodule

module TransicionJohnsonE1 (
  input  C0,
  input  C1,
  input  C2,
  input  C3,
  output S0,
  output S1,
  output S2,
  output S3
);

  wire and_1_out, and_2_out, and_3_out, and_4_out, and_5_out, and_6_out;

  and and_1 (and_1_out, ~C3, ~C2, C1);  // AND_Gate
  and and_2 (and_2_out, ~C3, C2, ~C1);  // AND_Gate
  and and_3 (and_3_out, ~C3, ~C2, C0);  // AND_Gate
  and and_4 (and_4_out, ~C3, C2, ~C1, ~C0);  // AND_Gate
  and and_5 (and_5_out, ~C3, ~C2, C1, C0);  // AND_Gate
  and and_6 (and_6_out, ~C3, C2, ~C0);  // AND_Gate
  and and_7 (S3, ~C3, C2);  // AND_Gate
  or or_1 (S1, and_1_out, and_2_out);
  or or_2 (S0, and_3_out, and_1_out, and_4_out);
  or or_3 (S2, and_2_out, and_5_out, and_6_out);
endmodule

module SecuenciadorBCDE2 (
);

  wire clock_1_out;
  wire [3:0] decodificarabcde2_1_bcd;
  wire [9:0] contadoranillo10bitse2_1_onehot;

  Clock clock_1 (.out(clock_1_out));
  ContadorAnillo10bitsE2 contadoranillo10bitse2_1 (.Clock(clock_1_out), .OneHot(contadoranillo10bitse2_1_onehot));
  Hex_Digit_Display hex_digit_display_1 (.value(decodificarabcde2_1_bcd));  // open: dp
  DecodificarABCDE2 decodificarabcde2_1 (.Entrada(contadoranillo10bitse2_1_onehot), .BCD(decodificarabcde2_1_bcd));
  LedBar #(.matrixcols(4)) ledbar_1 (
    .led0(decodificarabcde2_1_bcd[2]), .led1(decodificarabcde2_1_bcd[2]), .led2(decodificarabcde2_1_bcd[1]),
    .led3(decodificarabcde2_1_bcd[0]));
  // Digital_Oscilloscope digital_oscilloscope_1: pin names not known; wires that end beside it: clock_1_out, decodificarabcde2_1_bcd[0], decodificarabcde2_1_bcd[1], decodificarabcde2_1_bcd[2], decodificarabcde2_1_bcd[3]
endmodule

module ContadorAnillo10bitsE2 (
  input  Clock,
  output [9:0] OneHot
);

  wire por_1_out;

  POR por_1 (.out(por_1_out));
  D_Flip_Flop #(.trigger("falling")) d_ff_1 (
    .D(OneHot[0]), .clk(Clock), .Q(OneHot[9]), .preset(por_1_out));  // open: Qn, reset
  D_Flip_Flop #(.trigger("falling")) d_ff_2 (.D(OneHot[9]), .clk(Clock), .Q(OneHot[8]));  // open: Qn, preset, reset
  D_Flip_Flop #(.trigger("falling")) d_ff_3 (.D(OneHot[8]), .clk(Clock), .Q(OneHot[7]));  // open: Qn, preset, reset
  D_Flip_Flop #(.trigger("falling")) d_ff_4 (.D(OneHot[7]), .clk(Clock), .Q(OneHot[6]));  // open: Qn, preset, reset
  D_Flip_Flop #(.trigger("falling")) d_ff_5 (.D(OneHot[6]), .clk(Clock), .Q(OneHot[5]));  // open: Qn, preset, reset
  D_Flip_Flop #(.trigger("falling")) d_ff_6 (.D(OneHot[5]), .clk(Clock), .Q(OneHot[4]));  // open: Qn, preset, reset
  D_Flip_Flop #(.trigger("falling")) d_ff_7 (.D(OneHot[4]), .clk(Clock), .Q(OneHot[3]));  // open: Qn, preset, reset
  D_Flip_Flop #(.trigger("falling")) d_ff_8 (.D(OneHot[3]), .clk(Clock), .Q(OneHot[2]));  // open: Qn, preset, reset
  D_Flip_Flop #(.trigger("falling")) d_ff_9 (.D(OneHot[2]), .clk(Clock), .Q(OneHot[1]));  // open: Qn, preset, reset
  D_Flip_Flop #(.trigger("falling")) d_ff_10 (.D(OneHot[1]), .clk(Clock), .Q(OneHot[0]));  // open: Qn, preset, reset
endmodule

module DecodificarABCDE2 (
  input  [9:0] Entrada,
  output [3:0] BCD
);

  or or_1 (BCD[0], Entrada[0], Entrada[2], Entrada[4], Entrada[6], Entrada[8]);
  or or_2 (BCD[1], Entrada[1], Entrada[2], Entrada[5], Entrada[6]);
  or or_3 (BCD[2], Entrada[3], Entrada[4], Entrada[5], Entrada[6]);
  or or_4 (BCD[3], Entrada[7], Entrada[8]);

  // Other names for the same wires on the sheet: S0 = BCD[0]; S1 = BCD[1]; S2 = BCD[2]; S3 = BCD[3]; E0 = Entrada[0];
  //   E1 = Entrada[1]; E2 = Entrada[2]; E3 = Entrada[3]; E4 = Entrada[4]; E5 = Entrada[5]; E6 = Entrada[6];
  //   E7 = Entrada[7]; E8 = Entrada[8]; E9 = Entrada[9]
endmodule

module ContadorJohnson5BitsE3 (
);

  wire clock_1_out;
  wire [3:0] counter_1_q, digital_oscilloscope_1_p7;
  wire [4:0] transicionjohnsone3_1_s0;

  Clock clock_1 (.out(clock_1_out));
  Counter #(.max('h9), .width(4)) counter_1 (
    .Q(counter_1_q), .clk(clock_1_out));  // open: load, D, count, carry, up, clr
  TransicionJohnsonE3 transicionjohnsone3_1 (
    .C0(counter_1_q[0]), .C1(counter_1_q[1]), .C2(counter_1_q[2]), .C3(counter_1_q[3]),
    .S0(transicionjohnsone3_1_s0[0]), .S1(transicionjohnsone3_1_s0[1]), .S2(transicionjohnsone3_1_s0[2]),
    .S3(transicionjohnsone3_1_s0[3]), .S4(transicionjohnsone3_1_s0[4]));
  LedBar #(.matrixcols(5)) ledbar_1 (
    .led0(transicionjohnsone3_1_s0[4]), .led1(transicionjohnsone3_1_s0[3]),
    .led2(transicionjohnsone3_1_s0[2]), .led3(transicionjohnsone3_1_s0[1]), .led4(transicionjohnsone3_1_s0[0]));
  // Digital_Oscilloscope digital_oscilloscope_1: pin names not known; wires that end beside it: clock_1_out, transicionjohnsone3_1_s0[0], transicionjohnsone3_1_s0[1], transicionjohnsone3_1_s0[2], transicionjohnsone3_1_s0[3], transicionjohnsone3_1_s0[4], digital_oscilloscope_1_p7[0], digital_oscilloscope_1_p7[1], digital_oscilloscope_1_p7[2], digital_oscilloscope_1_p7[3]
  TransicionBCDAikenE3 transicionbcdaikene3_1 (.Johnson(transicionjohnsone3_1_s0), .Aiken(digital_oscilloscope_1_p7));
  LedBar #(.matrixcols(4)) ledbar_2 (
    .led0(digital_oscilloscope_1_p7[3]), .led1(digital_oscilloscope_1_p7[2]),
    .led2(digital_oscilloscope_1_p7[1]), .led3(digital_oscilloscope_1_p7[0]));
endmodule

module TransicionJohnsonE3 (
  input  C0,
  input  C1,
  input  C2,
  input  C3,
  output S0,
  output S1,
  output S2,
  output S3,
  output S4
);

  wire and_1_out, and_2_out, and_3_out, and_4_out, and_5_out, and_6_out, and_7_out, and_8_out, and_9_out,
       and_10_out, and_11_out, and_12_out, and_13_out;

  and and_1 (and_1_out, ~C3, ~C2, C0);  // AND_Gate
  and and_2 (and_2_out, ~C3, ~C2, C1);  // AND_Gate
  and and_3 (and_3_out, ~C3, C2, ~C1);  // AND_Gate
  and and_4 (and_4_out, ~C3, ~C2, C1);  // AND_Gate
  and and_5 (and_5_out, ~C3, C2, ~C1);  // AND_Gate
  and and_6 (and_6_out, ~C3, C1, ~C0);  // AND_Gate
  and and_7 (and_7_out, ~C3, C1, C0);  // AND_Gate
  and and_8 (and_8_out, ~C3, C2);  // AND_Gate
  and and_9 (and_9_out, C3, ~C2, ~C1, ~C0);  // AND_Gate
  and and_10 (and_10_out, ~C3, C2);  // AND_Gate
  and and_11 (and_11_out, ~C3, C2, C0);  // AND_Gate
  and and_12 (and_12_out, ~C3, C2, C1);  // AND_Gate
  and and_13 (and_13_out, C3, ~C2, ~C1);  // AND_Gate
  or or_1 (S0, and_1_out, and_2_out, and_3_out);
  or or_2 (S1, and_4_out, and_5_out, and_6_out);
  or or_3 (S2, and_7_out, and_8_out);
  or or_4 (S3, and_9_out, and_10_out);
  or or_5 (S4, and_11_out, and_12_out, and_13_out);
endmodule

module TransicionBCDAikenE3 (
  input  [4:0] Johnson,
  output [3:0] Aiken
);

  Multiplexer #(.select(5), .width(4)) multiplexer_1 (
    .in0(4'b0000), .in1(4'b0001), .in3(4'b0010), .in7(4'b0011), .in15(4'b0100), .in16(4'b1111),
    .in24(4'b1110), .in28(4'b1101), .in30(4'b1100), .in31(4'b1011), .out(Aiken), .sel(Johnson));  // open: in2, in4, in5, in6, in8, in9, in10, in11, in12, in13, in14, in17, in18, in19, in20, in21, in22, in23, in25, in26, in27, in29
endmodule

module PeriodicSignalGenE4 (
);

  wire clock_1_out, multiplexer_1_out;
  wire [2:0] counter_1_q, transicionjohnsone4_1_s0;

  Clock clock_1 (.out(clock_1_out));
  Counter #(.max('h5), .width(3)) counter_1 (
    .Q(counter_1_q), .clk(clock_1_out));  // open: load, D, count, carry, up, clr
  TransicionJohnsonE4 transicionjohnsone4_1 (
    .C0(counter_1_q[0]), .C1(counter_1_q[1]), .C2(counter_1_q[2]), .S0(transicionjohnsone4_1_s0[0]),
    .S1(transicionjohnsone4_1_s0[1]), .S2(transicionjohnsone4_1_s0[2]));
  LedBar #(.matrixcols(3)) ledbar_1 (
    .led0(transicionjohnsone4_1_s0[2]), .led1(transicionjohnsone4_1_s0[1]), .led2(transicionjohnsone4_1_s0[0]));
  Multiplexer #(.select(3)) multiplexer_1 (
    .in0(1'b1), .in1(1'b1), .in3(1'b0), .in4(1'b0), .in6(1'b0), .in7(1'b0), .out(multiplexer_1_out),
    .sel(transicionjohnsone4_1_s0));  // open: in2, in5
  // Digital_Oscilloscope digital_oscilloscope_1: pin names not known; wires that end beside it: clock_1_out, multiplexer_1_out
endmodule

module TransicionJohnsonE4 (
  input  C0,
  input  C1,
  input  C2,
  output S0,
  output S1,
  output S2
);

  wire and_1_out, and_2_out, and_3_out, and_4_out, and_5_out;

  and and_1 (and_1_out, C2, ~C1, ~C0);  // AND_Gate
  and and_2 (and_2_out, ~C2, C0);  // AND_Gate
  and and_3 (and_3_out, ~C1, C2);  // AND_Gate
  and and_4 (and_4_out, ~C2, C1);  // AND_Gate
  and and_5 (and_5_out, ~C2, C1, C0);  // AND_Gate
  or or_1 (S1, and_4_out, and_1_out);
  or or_2 (S0, and_4_out, and_2_out);
  or or_3 (S2, and_5_out, and_3_out);
endmodule

module FSME5 (
  input  A,
  output F
);

  wire and_1_out, and_2_out, and_3_out, and_4_out, and_5_out, and_6_out, Q0, Q1, S0, S1;

  and and_1 (and_1_out, ~S1, S0);  // AND_Gate
  and and_2 (and_2_out, S1, ~A);  // AND_Gate
  or or_1 (Q1, and_1_out, and_2_out);
  and and_3 (and_3_out, ~S0, A);  // AND_Gate
  and and_4 (and_4_out, ~S1, S0, ~A);  // AND_Gate
  and and_5 (and_5_out, S1, ~A);  // AND_Gate
  and and_6 (and_6_out, ~S1, S0, A);  // AND_Gate
  or or_2 (Q0, and_3_out, and_4_out);
  or or_3 (F, and_5_out, and_6_out);
  D_Flip_Flop #(.trigger("falling")) d_ff_1 (.D(Q1), .clk(A), .Q(S1));  // open: Qn, preset, reset
  D_Flip_Flop #(.trigger("falling")) d_ff_2 (.D(Q0), .clk(A), .Q(S0));  // open: Qn, preset, reset
endmodule

module FSME6 (
  input  A,
  output out_2
);

  wire and_1_out, and_2_out, and_3_out, and_4_out, and_5_out, Q0, Q1, S0, S1;

  and and_1 (and_1_out, S1, ~A);  // AND_Gate
  and and_2 (and_2_out, S1, ~S0);  // AND_Gate
  and and_3 (and_3_out, ~S1, S0, A);  // AND_Gate
  and and_4 (and_4_out, ~S0, A);  // AND_Gate
  and and_5 (and_5_out, ~S1, S0, ~A);  // AND_Gate
  or or_1 (out_2, S1, ~S0);  // OR_Gate
  or or_2 (Q1, and_1_out, and_2_out, and_3_out);
  or or_3 (Q0, and_4_out, and_5_out);
  D_Flip_Flop #(.trigger("falling")) d_ff_1 (.D(Q1), .clk(A), .Q(S1));  // open: Qn, preset, reset
  LED led_1 (.in(S1));
  LED led_2 (.in(S0));
  D_Flip_Flop #(.trigger("falling")) d_ff_2 (.D(Q0), .clk(A), .Q(S0));  // open: Qn, preset, reset

  // Other names for the same wires on the sheet: F = out_2
endmodule

module MaquinaDeGaseosasE7 (
  input  A1,
  input  A0,
  input  Reset,
  output G
);

  wire A0_t, A1_t, Clock, or_1_out, or_2_out, or_3_out, or_4_out, or_5_out, Q0, Q1, S0, S1, undriven;

  Clock clock_1 (.out(Clock));
  and and_1 (A1_t, A1, Clock);
  and and_2 (A0_t, Clock, A0);
  or or_1 (or_1_out, S1, S0, A1_t);
  or or_2 (or_2_out, S1, A1_t, A0_t);
  or or_3 (or_3_out, S1, S0, A0_t);
  or or_4 (or_4_out, S0, A1_t, A0_t);
  or or_5 (or_5_out, S1, ~S0, A1_t, ~A0_t);  // OR_Gate
  and and_3 (G, S1, S0);
  and and_4 (Q1, or_1_out, or_2_out);
  and and_5 (Q0, or_3_out, or_4_out, or_5_out);
  D_Flip_Flop #(.trigger("falling")) d_ff_1 (.D(Q1), .clk(undriven), .Q(S1), .reset(Reset));  // open: Qn, preset
  LED led_1 (.in(S1));
  LED led_2 (.in(S0));
  D_Flip_Flop #(.trigger("falling")) d_ff_2 (.D(Q0), .clk(undriven), .Q(S0), .reset(Reset));  // open: Qn, preset
endmodule

module ContadorBinarioSinc3BitsE8 (
);

  wire and_1_out, and_2_out, and_3_out, and_4_out, and_5_out, clock_1_out, Q0, Q1, Q2, S0, S1, S2;

  not not_1 (Q0, S0);
  and and_1 (and_1_out, ~S2, ~S1, ~S0);  // AND_Gate
  and and_2 (and_2_out, S2, S1);
  and and_3 (and_3_out, S2, S0);
  and and_4 (and_4_out, S0, S1);
  and and_5 (and_5_out, ~S0, ~S1);  // AND_Gate
  or or_1 (Q1, and_4_out, and_5_out);
  or or_2 (Q2, and_1_out, and_2_out, and_3_out);
  Clock clock_1 (.out(clock_1_out));
  D_Flip_Flop d_ff_1 (.D(Q0), .clk(clock_1_out), .Q(S0));  // open: Qn, preset, reset
  D_Flip_Flop d_ff_2 (.D(Q1), .clk(clock_1_out), .Q(S1));  // open: Qn, preset, reset
  D_Flip_Flop d_ff_3 (.D(Q2), .clk(clock_1_out), .Q(S2));  // open: Qn, preset, reset
  LedBar #(.matrixcols(3)) ledbar_1 (.led0(S2), .led1(S1), .led2(S0));
endmodule

module SemaforoProgramableE9 (
);

  wire A1, A2, and_1_out, Clear, Clock, E0, E1, E2, E3, or_1_out, Q0, Q1, R2, Reset, V1, V2;
  wire [1:0] Estado;
  wire [3:0] counter_1_q;

  Clock clock_1 (.out(Clock));
  and and_1 (and_1_out, Clock, Clear);
  Counter #(.max('hf), .width(4)) counter_1 (
    .Q(counter_1_q), .clk(Clock), .clr(or_1_out));  // open: load, D, count, carry, up
  or or_1 (or_1_out, and_1_out, Reset);
  POR por_1 (.out(Reset));
  ContadorBinarioSinc4BitsE9 contadorbinariosinc4bitse9_1 (
    .Reset(Reset), .Clear(Clear), .Clock(Clock), .E0(E0), .E1(E1), .E2(E2), .E3(E3));
  Hex_Digit_Display hex_digit_display_1 (.value(counter_1_q));  // open: dp
  ROM #(.addrWidth(6), .dataWidth(3), .misaligned("true")) rom_1 (
    .addr({Estado, E3, E2, E1, E0}), .data({Clear, Q1, Q0}));
  D_Flip_Flop d_ff_1 (.D(Q0), .clk(Clock), .Q(Estado[0]));  // open: Qn, preset, reset
  D_Flip_Flop d_ff_2 (.D(Q1), .clk(Clock), .Q(Estado[1]));  // open: Qn, preset, reset
  not not_1 (R2, Estado[1]);
  and and_2 (A1, ~Estado[1], Estado[0]);  // AND_Gate
  and and_3 (A2, Estado[1], Estado[0]);
  and and_4 (V1, ~Estado[1], ~Estado[0]);  // AND_Gate
  and and_5 (V2, Estado[1], ~Estado[0]);  // AND_Gate
  LED led_1 (.in(Estado[1]));
  LED led_2 (.in(A1));
  LED led_3 (.in(V1));
  LED led_4 (.in(R2));
  LED led_5 (.in(A2));
  LED led_6 (.in(V2));

  // Other names for the same wires on the sheet: S0 = Estado[0]; R1 = Estado[1]; S1 = Estado[1]

  // Notes on the sheet:
  //   contents of rom_1 (hex, n*v repeats v):
  //   11*0 5 4*0 4*1 6 11*0 13*2 7 0 0 3 4
endmodule

module TecladoCajaFuerteE10 (
  output Abierto
);

  wire Clock, D0, D1, D2, D3, D4, D5, D6, D7, D8, D9, DA, E0, E1, E2, E3, por_1_out, Q0, Q1, Q2, S0, S1, S2;

  Button button_1 (.out(D7));
  Button button_2 (.out(D4));
  Button button_3 (.out(D1));
  Button button_4 (.out(D0));
  Button button_5 (.out(D8));
  Button button_6 (.out(D5));
  Button button_7 (.out(D2));
  Button button_8 (.out(DA));
  EncoderE9 encodere9_1 (
    .D0(D0), .D1(D1), .D2(D2), .D3(D3), .D4(D4), .D5(D5), .D6(D6), .D7(D7), .D8(D8), .D9(D9), .DA(DA),
    .E0(E0), .E1(E1), .E2(E2), .E3(E3), .Clock(Clock));
  Button button_9 (.out(D9));
  Button button_10 (.out(D6));
  Button button_11 (.out(D3));
  ROM #(.addrWidth(7), .dataWidth(4)) rom_1 (.addr({S2, S1, S0, E3, E2, E1, E0}), .data({Abierto, Q2, Q1, Q0}));
  D_Flip_Flop #(.trigger("falling")) d_ff_1 (.D(Q0), .clk(Clock), .Q(S0), .reset(por_1_out));  // open: Qn, preset
  D_Flip_Flop #(.trigger("falling")) d_ff_2 (.D(Q1), .clk(Clock), .Q(S1), .reset(por_1_out));  // open: Qn, preset
  D_Flip_Flop #(.trigger("falling")) d_ff_3 (.D(Q2), .clk(Clock), .Q(S2), .reset(por_1_out));  // open: Qn, preset
  POR por_1 (.out(por_1_out));
  LED led_1 (.in(Abierto));
  Hex_Digit_Display hex_digit_display_1 (.value({1'b0, S2, S1, S0}));  // open: dp

  // Notes on the sheet:
  //   contents of rom_1 (hex, n*v repeats v):
  //   10*0 1 5*0 4*6 2 5*6 1 5*0 3 9*6 1 5*0 7*6 4 6 6 1 5*0 8*6 5 6 1 5*0 10*e 9 5*0 10*6 1
endmodule

module ContadorBinarioSinc4BitsE9 (
  input  Reset,
  input  Clear,
  input  Clock,
  output E0,
  output E1,
  output E2,
  output E3
);

  wire and_1_out, and_2_out, and_3_out, and_4_out, and_5_out, and_6_out, and_7_out, and_8_out, and_9_out,
       and_10_out, and_11_out, Q0, Q1, Q2, Q3;

  not not_1 (Q0, E0);
  and and_1 (and_1_out, ~E2, E1, E0);  // AND_Gate
  and and_2 (and_2_out, E2, ~E1);  // AND_Gate
  and and_3 (and_3_out, E2, ~E0);  // AND_Gate
  xor xor_1 (Q1, E0, E1);
  and and_4 (and_4_out, ~E3, E2, E1, E0);  // AND_Gate
  and and_5 (and_5_out, E3, ~E2);  // AND_Gate
  and and_6 (and_6_out, E3, ~E1);  // AND_Gate
  and and_7 (and_7_out, E3, ~E0);  // AND_Gate
  or or_1 (Q2, and_1_out, and_2_out, and_3_out);
  or or_2 (Q3, and_4_out, and_5_out, and_6_out, and_7_out);
  D_Flip_Flop d_ff_1 (.D(and_8_out), .clk(Clock), .Q(E0), .reset(Reset));  // open: Qn, preset
  and and_8 (and_8_out, Q0, ~Clear);  // AND_Gate
  D_Flip_Flop d_ff_2 (.D(and_9_out), .clk(Clock), .Q(E1), .reset(Reset));  // open: Qn, preset
  and and_9 (and_9_out, Q1, ~Clear);  // AND_Gate
  D_Flip_Flop d_ff_3 (.D(and_10_out), .clk(Clock), .Q(E2), .reset(Reset));  // open: Qn, preset
  and and_10 (and_10_out, Q2, ~Clear);  // AND_Gate
  D_Flip_Flop d_ff_4 (.D(and_11_out), .clk(Clock), .Q(E3), .reset(Reset));  // open: Qn, preset
  and and_11 (and_11_out, Q3, ~Clear);  // AND_Gate
  Hex_Digit_Display hex_digit_display_1 (.value({E3, E2, E1, E0}));  // open: dp

  // Other names for the same wires on the sheet: S0 = E0; S1 = E1; S2 = E2; S3 = E3
endmodule

module EncoderE9 (
  input  D0,
  input  D1,
  input  D2,
  input  D3,
  input  D4,
  input  D5,
  input  D6,
  input  D7,
  input  D8,
  input  D9,
  input  DA,
  output E0,
  output E1,
  output E2,
  output E3,
  output Clock
);

  or or_1 (Clock, D0, D1, D2, D3, D4, DA, D5, D6, D7, D8, D9);
  or or_2 (E0, D1, D3, D5, D7, D9);
  or or_3 (E3, D8, D9, DA);
  or or_4 (E1, D2, D3, D6, D7, DA);
  or or_5 (E2, D4, D5, D6, D7);
endmodule

module TermometroE10 (
  input  Reset
);

  wire Alarma, clock_1_out, Q, S;
  wire [3:0] Calor;

  Clock clock_1 (.out(clock_1_out));
  Slider #(.width(4)) Termometro (.out(Calor));
  D_Flip_Flop d_ff_1 (.D(Q), .clk(clock_1_out), .Q(S), .reset(Reset));  // open: Qn, preset
  ROM #(.addrWidth(5), .dataWidth(2)) rom_1 (.addr({S, Calor}), .data({Alarma, Q}));
  // Buzzer buzzer_1: pin names not known; wires that end beside it: 14'hff, Alarma, 7'b0000111
  LED led_1 (.in(Alarma));

  // Notes on the sheet:
  //   contents of rom_1 (hex, n*v repeats v):
  //   12*0 3 11*0 2 7*3
endmodule

module ContadorSincBinarioAsc3BitsE12 (
);

  wire clock_1_out, multiplexer_1_out, multiplexer_2_out, multiplexer_3_out;
  wire [2:0] S;

  Multiplexer #(.select(3)) multiplexer_1 (
    .in0(1'b0), .in1(1'b0), .in2(1'b0), .in3(1'b1), .in4(1'b1), .in5(1'b1), .in6(1'b1), .in7(1'b0),
    .out(multiplexer_1_out), .sel(S));
  Clock clock_1 (.out(clock_1_out));
  D_Flip_Flop d_ff_1 (.D(multiplexer_1_out), .clk(clock_1_out), .Q(S[2]));  // open: Qn, preset, reset
  Multiplexer #(.select(3)) multiplexer_2 (
    .in0(1'b0), .in1(1'b1), .in2(1'b1), .in3(1'b0), .in4(1'b0), .in5(1'b1), .in6(1'b1), .in7(1'b0),
    .out(multiplexer_2_out), .sel(S));
  D_Flip_Flop d_ff_2 (.D(multiplexer_2_out), .clk(clock_1_out), .Q(S[1]));  // open: Qn, preset, reset
  Multiplexer #(.select(3)) multiplexer_3 (
    .in0(1'b1), .in1(1'b0), .in2(1'b1), .in3(1'b0), .in4(1'b1), .in5(1'b0), .in6(1'b1), .in7(1'b0),
    .out(multiplexer_3_out), .sel(S));
  D_Flip_Flop d_ff_3 (.D(multiplexer_3_out), .clk(clock_1_out), .Q(S[0]));  // open: Qn, preset, reset
  Hex_Digit_Display hex_digit_display_1 (.value({1'b0, S}));  // open: dp
endmodule

module ContadorSincBinarioDsc3BitsE13 (
);

  wire clock_1_out, multiplexer_1_out, multiplexer_2_out, multiplexer_3_out;
  wire [2:0] S;

  Multiplexer #(.select(3)) multiplexer_1 (
    .in0(1'b1), .in1(1'b0), .in2(1'b0), .in3(1'b0), .in4(1'b0), .in5(1'b1), .in6(1'b1), .in7(1'b1),
    .out(multiplexer_1_out), .sel(S));
  Clock clock_1 (.out(clock_1_out));
  D_Flip_Flop d_ff_1 (.D(multiplexer_1_out), .clk(clock_1_out), .Q(S[2]));  // open: Qn, preset, reset
  Multiplexer #(.select(3)) multiplexer_2 (
    .in0(1'b1), .in1(1'b0), .in2(1'b0), .in3(1'b1), .in4(1'b1), .in5(1'b0), .in6(1'b0), .in7(1'b1),
    .out(multiplexer_2_out), .sel(S));
  D_Flip_Flop d_ff_2 (.D(multiplexer_2_out), .clk(clock_1_out), .Q(S[1]));  // open: Qn, preset, reset
  Multiplexer #(.select(3)) multiplexer_3 (
    .in0(1'b1), .in1(1'b0), .in2(1'b1), .in3(1'b0), .in4(1'b1), .in5(1'b0), .in6(1'b1), .in7(1'b0),
    .out(multiplexer_3_out), .sel(S));
  D_Flip_Flop d_ff_3 (.D(multiplexer_3_out), .clk(clock_1_out), .Q(S[0]));  // open: Qn, preset, reset
  Hex_Digit_Display hex_digit_display_1 (.value({1'b0, S}));  // open: dp
endmodule

module ContadorSincBinarioMod5E14 (
);

  wire clock_1_out, multiplexer_1_out, multiplexer_2_out, multiplexer_3_out;
  wire [2:0] S;

  // DipSwitch dipswitch_1: pin names not known
  Multiplexer #(.select(3)) multiplexer_1 (
    .out(multiplexer_1_out), .sel(S));  // open: in0, in1, in2, in3, in4, in5, in6, in7
  Clock clock_1 (.out(clock_1_out));
  D_Flip_Flop d_ff_1 (.D(multiplexer_1_out), .clk(clock_1_out), .Q(S[2]));  // open: Qn, preset, reset
  // DipSwitch dipswitch_2: pin names not known
  Multiplexer #(.select(3)) multiplexer_2 (
    .out(multiplexer_2_out), .sel(S));  // open: in0, in1, in2, in3, in4, in5, in6, in7
  D_Flip_Flop d_ff_2 (.D(multiplexer_2_out), .clk(clock_1_out), .Q(S[1]));  // open: Qn, preset, reset
  // DipSwitch dipswitch_3: pin names not known
  Multiplexer #(.select(3)) multiplexer_3 (
    .out(multiplexer_3_out), .sel(S));  // open: in0, in1, in2, in3, in4, in5, in6, in7
  D_Flip_Flop d_ff_3 (.D(multiplexer_3_out), .clk(clock_1_out), .Q(S[0]));  // open: Qn, preset, reset
  Hex_Digit_Display hex_digit_display_1 (.value({1'b0, S}));  // open: dp
endmodule

module FSME15 (
  input  A,
  output F
);

  wire clock_1_out, multiplexer_1_out, multiplexer_3_out, S0, S1;

  // DipSwitch dipswitch_1: pin names not known
  D_Flip_Flop d_ff_1 (.D(multiplexer_1_out), .clk(clock_1_out), .Q(S0));  // open: Qn, preset, reset
  Multiplexer #(.select(3)) multiplexer_1 (
    .out(multiplexer_1_out), .sel({S1, S0, A}));  // open: in0, in1, in2, in3, in4, in5, in6, in7
  Clock clock_1 (.out(clock_1_out));
  // DipSwitch #(.number(4)) dipswitch_2: pin names not known
  Multiplexer #(.select(2)) multiplexer_2 (.out(F), .sel({S1, S0}));  // open: in0, in1, in2, in3
  // DipSwitch dipswitch_3: pin names not known
  Multiplexer #(.select(3)) multiplexer_3 (
    .out(multiplexer_3_out), .sel({S1, S0, A}));  // open: in0, in1, in2, in3, in4, in5, in6, in7
  D_Flip_Flop d_ff_2 (.D(multiplexer_3_out), .clk(clock_1_out), .Q(S1));  // open: Qn, preset, reset
endmodule
