// Logisim project TPunidad4.circ as structural Verilog
module main (
  input  Enable,
  input  [7:0] Entrada,
  output [7:0] Salida
);

  wire [3:0] mostrardoshexa_1_digito1, mostrardoshexa_1_digito2, mostrardoshexa_2_digito1,
       mostrardoshexa_2_digito2;

  MostrarDosHexa mostrardoshexa_1 (
    .Entrada(Entrada), .Digito1(mostrardoshexa_1_digito1), .Digito2(mostrardoshexa_1_digito2));
  Hex_Digit_Display hex_digit_display_1 (.value(mostrardoshexa_1_digito2));  // open: dp
  Hex_Digit_Display hex_digit_display_2 (.value(mostrardoshexa_1_digito1));  // open: dp
  FlipFlopDSincronicoPorNivel flipflopdsincronicopornivel_1 (.D(Entrada[0]), .E(Enable), .Q(Salida[0]));  // open: NotQ
  FlipFlopDSincronicoPorNivel flipflopdsincronicopornivel_2 (.D(Entrada[1]), .E(Enable), .Q(Salida[1]));  // open: NotQ
  FlipFlopDSincronicoPorNivel flipflopdsincronicopornivel_3 (.D(Entrada[2]), .E(Enable), .Q(Salida[2]));  // open: NotQ
  FlipFlopDSincronicoPorNivel flipflopdsincronicopornivel_4 (.D(Entrada[3]), .E(Enable), .Q(Salida[3]));  // open: NotQ
  FlipFlopDSincronicoPorNivel flipflopdsincronicopornivel_5 (.D(Entrada[4]), .E(Enable), .Q(Salida[4]));  // open: NotQ
  FlipFlopDSincronicoPorNivel flipflopdsincronicopornivel_6 (.D(Entrada[5]), .E(Enable), .Q(Salida[5]));  // open: NotQ
  FlipFlopDSincronicoPorNivel flipflopdsincronicopornivel_7 (.D(Entrada[6]), .E(Enable), .Q(Salida[6]));  // open: NotQ
  FlipFlopDSincronicoPorNivel flipflopdsincronicopornivel_8 (.D(Entrada[7]), .E(Enable), .Q(Salida[7]));  // open: NotQ
  Hex_Digit_Display hex_digit_display_3 (.value(mostrardoshexa_2_digito2));  // open: dp
  MostrarDosHexa mostrardoshexa_2 (
    .Entrada(Salida), .Digito1(mostrardoshexa_2_digito1), .Digito2(mostrardoshexa_2_digito2));
  Hex_Digit_Display hex_digit_display_4 (.value(mostrardoshexa_2_digito1));  // open: dp
endmodule

module FlipFlopDSincronicoPorNivel (
  input  D,
  input  E,
  output Q,
  output NotQ
);

  wire and_1_out, and_2_out;

  and and_1 (and_1_out, ~D, E);  // AND_Gate
  and and_2 (and_2_out, E, D);
  nor nor_1 (Q, and_1_out, NotQ);
  nor nor_2 (NotQ, Q, and_2_out);
endmodule

module MostrarDosHexa (
  input  [7:0] Entrada,
  output [3:0] Digito1,
  output [3:0] Digito2
);


  assign Digito1 = Entrada[3:0];
  assign Digito2 = Entrada[7:4];
endmodule

module Registro8bits1 (
  input  Enable,
  input  [7:0] Entrada,
  output [7:0] Salida
);

  wire [3:0] mostrardoshexa_1_digito1, mostrardoshexa_1_digito2, mostrardoshexa_2_digito1,
       mostrardoshexa_2_digito2;

  MostrarDosHexa mostrardoshexa_1 (
    .Entrada(Entrada), .Digito1(mostrardoshexa_1_digito1), .Digito2(mostrardoshexa_1_digito2));
  Hex_Digit_Display hex_digit_display_1 (.value(mostrardoshexa_1_digito2));  // open: dp
  Hex_Digit_Display hex_digit_display_2 (.value(mostrardoshexa_1_digito1));  // open: dp
  FlipFlopDSincronicoPorNivel flipflopdsincronicopornivel_1 (.D(Entrada[0]), .E(Enable), .Q(Salida[0]));  // open: NotQ
  FlipFlopDSincronicoPorNivel flipflopdsincronicopornivel_2 (.D(Entrada[1]), .E(Enable), .Q(Salida[1]));  // open: NotQ
  FlipFlopDSincronicoPorNivel flipflopdsincronicopornivel_3 (.D(Entrada[2]), .E(Enable), .Q(Salida[2]));  // open: NotQ
  FlipFlopDSincronicoPorNivel flipflopdsincronicopornivel_4 (.D(Entrada[3]), .E(Enable), .Q(Salida[3]));  // open: NotQ
  FlipFlopDSincronicoPorNivel flipflopdsincronicopornivel_5 (.D(Entrada[4]), .E(Enable), .Q(Salida[4]));  // open: NotQ
  FlipFlopDSincronicoPorNivel flipflopdsincronicopornivel_6 (.D(Entrada[5]), .E(Enable), .Q(Salida[5]));  // open: NotQ
  FlipFlopDSincronicoPorNivel flipflopdsincronicopornivel_7 (.D(Entrada[6]), .E(Enable), .Q(Salida[6]));  // open: NotQ
  FlipFlopDSincronicoPorNivel flipflopdsincronicopornivel_8 (.D(Entrada[7]), .E(Enable), .Q(Salida[7]));  // open: NotQ
  Hex_Digit_Display hex_digit_display_3 (.value(mostrardoshexa_2_digito2));  // open: dp
  MostrarDosHexa mostrardoshexa_2 (
    .Entrada(Salida), .Digito1(mostrardoshexa_2_digito1), .Digito2(mostrardoshexa_2_digito2));
  Hex_Digit_Display hex_digit_display_4 (.value(mostrardoshexa_2_digito1));  // open: dp
endmodule

module SumadorConLatches2 (
  input  ClockA,
  input  [7:0] A,
  input  ClockSalida,
  input  ClockB,
  input  [7:0] B,
  input  Reset
);

  wire [3:0] mostrardoshexa_1_digito1, mostrardoshexa_1_digito2, mostrardoshexa_2_digito1,
       mostrardoshexa_2_digito2, mostrardoshexa_3_digito1, mostrardoshexa_3_digito2,
       mostrardoshexa_4_digito1, mostrardoshexa_4_digito2, mostrardoshexa_5_digito1,
       mostrardoshexa_5_digito2, mostrardoshexa_6_digito1, mostrardoshexa_6_digito2;
  wire [7:0] registro8bits1_1_salida, registro8bits1_2_salida, registro8bits1_3_salida, sumador8bits_1_sum;

  Hex_Digit_Display hex_digit_display_1 (.value(mostrardoshexa_1_digito2));  // open: dp
  MostrarDosHexa mostrardoshexa_1 (.Entrada(A), .Digito1(mostrardoshexa_1_digito1), .Digito2(mostrardoshexa_1_digito2));
  Hex_Digit_Display hex_digit_display_2 (.value(mostrardoshexa_2_digito2));  // open: dp
  MostrarDosHexa mostrardoshexa_2 (.Entrada(B), .Digito1(mostrardoshexa_2_digito1), .Digito2(mostrardoshexa_2_digito2));
  Hex_Digit_Display hex_digit_display_3 (.value(mostrardoshexa_1_digito1));  // open: dp
  Hex_Digit_Display hex_digit_display_4 (.value(mostrardoshexa_2_digito1));  // open: dp
  Registro8bits1 registro8bits1_1 (.Enable(ClockA), .Entrada(A), .Salida(registro8bits1_1_salida));
  Registro8bits1 registro8bits1_2 (.Enable(ClockB), .Entrada(B), .Salida(registro8bits1_2_salida));
  MostrarDosHexa mostrardoshexa_3 (
    .Entrada(registro8bits1_1_salida), .Digito1(mostrardoshexa_3_digito1), .Digito2(mostrardoshexa_3_digito2));
  MostrarDosHexa mostrardoshexa_4 (
    .Entrada(registro8bits1_2_salida), .Digito1(mostrardoshexa_4_digito1), .Digito2(mostrardoshexa_4_digito2));
  Hex_Digit_Display hex_digit_display_5 (.value(mostrardoshexa_3_digito2));  // open: dp
  Hex_Digit_Display hex_digit_display_6 (.value(mostrardoshexa_4_digito1));  // open: dp
  Hex_Digit_Display hex_digit_display_7 (.value(mostrardoshexa_4_digito2));  // open: dp
  Hex_Digit_Display hex_digit_display_8 (.value(mostrardoshexa_3_digito1));  // open: dp
  Sumador8bits sumador8bits_1 (
    .A(registro8bits1_1_salida), .B(registro8bits1_2_salida), .Sum(sumador8bits_1_sum));  // open: Cout
  MostrarDosHexa mostrardoshexa_5 (
    .Entrada(sumador8bits_1_sum), .Digito1(mostrardoshexa_5_digito1), .Digito2(mostrardoshexa_5_digito2));
  Hex_Digit_Display hex_digit_display_9 (.value(mostrardoshexa_5_digito2));  // open: dp
  Hex_Digit_Display hex_digit_display_10 (.value(mostrardoshexa_5_digito1));  // open: dp
  Registro8bits1 registro8bits1_3 (
    .Enable(ClockSalida), .Entrada(sumador8bits_1_sum), .Salida(registro8bits1_3_salida));
  MostrarDosHexa mostrardoshexa_6 (
    .Entrada(registro8bits1_3_salida), .Digito1(mostrardoshexa_6_digito1), .Digito2(mostrardoshexa_6_digito2));
  Hex_Digit_Display hex_digit_display_11 (.value(mostrardoshexa_6_digito2));  // open: dp
  Hex_Digit_Display hex_digit_display_12 (.value(mostrardoshexa_6_digito1));  // open: dp

  assign Reset = ClockSalida;
endmodule

module FlipFlopDSincronicoPorFlanco (
  input  D,
  input  E,
  output Q,
  output NotQ
);

  wire and_1_out, and_2_out, and_3_out, not_1_out, not_2_out, not_3_out;

  not not_1 (not_1_out, E);
  not not_2 (not_2_out, not_1_out);
  not not_3 (not_3_out, not_2_out);
  and and_1 (and_1_out, E, not_3_out);
  and and_2 (and_2_out, ~D, and_1_out);  // AND_Gate
  and and_3 (and_3_out, and_1_out, D);
  nor nor_1 (Q, and_2_out, NotQ);
  nor nor_2 (NotQ, Q, and_3_out);
endmodule

module Sumador8bits (
  input  [7:0] A,
  input  [7:0] B,
  output [7:0] Sum,
  output Cout
);

  wire semisumador_1_carry, sumadorcompleto_1_carryout, sumadorcompleto_2_carryout,
       sumadorcompleto_3_carryout, sumadorcompleto_4_carryout, sumadorcompleto_5_carryout,
       sumadorcompleto_6_carryout;

  SemiSumador semisumador_1 (.A(A[0]), .B(B[0]), .Suma(Sum[0]), .Carry(semisumador_1_carry));
  SumadorCompleto sumadorcompleto_1 (
    .A(A[1]), .B(B[1]), .CarryIn(semisumador_1_carry), .Suma(Sum[1]), .CarryOut(sumadorcompleto_1_carryout));
  SumadorCompleto sumadorcompleto_2 (
    .A(A[2]), .B(B[2]), .CarryIn(sumadorcompleto_1_carryout), .Suma(Sum[2]),
    .CarryOut(sumadorcompleto_2_carryout));
  SumadorCompleto sumadorcompleto_3 (
    .A(A[3]), .B(B[3]), .CarryIn(sumadorcompleto_2_carryout), .Suma(Sum[3]),
    .CarryOut(sumadorcompleto_3_carryout));
  SumadorCompleto sumadorcompleto_4 (
    .A(A[4]), .B(B[4]), .CarryIn(sumadorcompleto_3_carryout), .Suma(Sum[4]),
    .CarryOut(sumadorcompleto_4_carryout));
  SumadorCompleto sumadorcompleto_5 (
    .A(A[5]), .B(B[5]), .CarryIn(sumadorcompleto_4_carryout), .Suma(Sum[5]),
    .CarryOut(sumadorcompleto_5_carryout));
  SumadorCompleto sumadorcompleto_6 (
    .A(A[6]), .B(B[6]), .CarryIn(sumadorcompleto_5_carryout), .Suma(Sum[6]),
    .CarryOut(sumadorcompleto_6_carryout));
  SumadorCompleto sumadorcompleto_7 (
    .A(A[7]), .B(B[7]), .CarryIn(sumadorcompleto_6_carryout), .Suma(Sum[7]), .CarryOut(Cout));
endmodule

module SemiSumador (
  input  A,
  input  B,
  output Suma,
  output Carry
);

  xor xor_1 (Suma, A, B);
  and and_1 (Carry, A, B);
endmodule

module SumadorCompleto (
  input  A,
  input  B,
  input  CarryIn,
  output Suma,
  output CarryOut
);

  wire and_1_out, and_2_out, and_3_out, xor_1_out;

  xor xor_1 (xor_1_out, A, B);
  and and_1 (and_1_out, A, B);
  and and_2 (and_2_out, A, CarryIn);
  and and_3 (and_3_out, B, CarryIn);
  xor xor_2 (Suma, xor_1_out, CarryIn);
  or or_1 (CarryOut, and_1_out, and_2_out, and_3_out);
endmodule

module Registro8bits2 (
  input  Enable,
  input  [7:0] Entrada,
  output [7:0] Salida
);

  wire [3:0] mostrardoshexa_1_digito1, mostrardoshexa_1_digito2, mostrardoshexa_2_digito1,
       mostrardoshexa_2_digito2;

  MostrarDosHexa mostrardoshexa_1 (
    .Entrada(Entrada), .Digito1(mostrardoshexa_1_digito1), .Digito2(mostrardoshexa_1_digito2));
  Hex_Digit_Display hex_digit_display_1 (.value(mostrardoshexa_1_digito2));  // open: dp
  Hex_Digit_Display hex_digit_display_2 (.value(mostrardoshexa_1_digito1));  // open: dp
  FlipFlopDSincronicoPorFlanco flipflopdsincronicoporflanco_1 (
    .D(Entrada[0]), .E(Enable), .Q(Salida[0]));  // open: NotQ
  FlipFlopDSincronicoPorFlanco flipflopdsincronicoporflanco_2 (
    .D(Entrada[1]), .E(Enable), .Q(Salida[1]));  // open: NotQ
  FlipFlopDSincronicoPorFlanco flipflopdsincronicoporflanco_3 (
    .D(Entrada[2]), .E(Enable), .Q(Salida[2]));  // open: NotQ
  FlipFlopDSincronicoPorFlanco flipflopdsincronicoporflanco_4 (
    .D(Entrada[3]), .E(Enable), .Q(Salida[3]));  // open: NotQ
  FlipFlopDSincronicoPorFlanco flipflopdsincronicoporflanco_5 (
    .D(Entrada[4]), .E(Enable), .Q(Salida[4]));  // open: NotQ
  FlipFlopDSincronicoPorFlanco flipflopdsincronicoporflanco_6 (
    .D(Entrada[5]), .E(Enable), .Q(Salida[5]));  // open: NotQ
  FlipFlopDSincronicoPorFlanco flipflopdsincronicoporflanco_7 (
    .D(Entrada[6]), .E(Enable), .Q(Salida[6]));  // open: NotQ
  FlipFlopDSincronicoPorFlanco flipflopdsincronicoporflanco_8 (
    .D(Entrada[7]), .E(Enable), .Q(Salida[7]));  // open: NotQ
  Hex_Digit_Display hex_digit_display_3 (.value(mostrardoshexa_2_digito2));  // open: dp
  MostrarDosHexa mostrardoshexa_2 (
    .Entrada(Salida), .Digito1(mostrardoshexa_2_digito1), .Digito2(mostrardoshexa_2_digito2));
  Hex_Digit_Display hex_digit_display_4 (.value(mostrardoshexa_2_digito1));  // open: dp
endmodule

module PruebaSincronismo (
);

  FlipFlopDSincronicoPorNivel flipflopdsincronicopornivel_1 ();  // open: D, E, Q, NotQ
endmodule

module Latch8bits (
  input  Enable,
  input  [7:0] Entrada,
  input  Reset,
  output [7:0] Salida
);

  wire and_1_out, and_2_out, and_3_out, and_4_out, and_5_out, and_6_out, and_7_out, and_8_out, or_1_out;
  wire [3:0] mostrardoshexa_1_digito1, mostrardoshexa_1_digito2, mostrardoshexa_2_digito1,
       mostrardoshexa_2_digito2;

  MostrarDosHexa mostrardoshexa_1 (
    .Entrada(Entrada), .Digito1(mostrardoshexa_1_digito1), .Digito2(mostrardoshexa_1_digito2));
  Hex_Digit_Display hex_digit_display_1 (.value(mostrardoshexa_1_digito2));  // open: dp
  Hex_Digit_Display hex_digit_display_2 (.value(mostrardoshexa_1_digito1));  // open: dp
  and and_1 (and_1_out, Entrada[0], ~Reset);  // AND_Gate
  and and_2 (and_2_out, Entrada[1], ~Reset);  // AND_Gate
  and and_3 (and_3_out, Entrada[2], ~Reset);  // AND_Gate
  and and_4 (and_4_out, Entrada[3], ~Reset);  // AND_Gate
  and and_5 (and_5_out, Entrada[4], ~Reset);  // AND_Gate
  and and_6 (and_6_out, Entrada[5], ~Reset);  // AND_Gate
  and and_7 (and_7_out, Entrada[6], ~Reset);  // AND_Gate
  and and_8 (and_8_out, Entrada[7], ~Reset);  // AND_Gate
  or or_1 (or_1_out, Enable, Reset);
  FlipFlopDSincronicoPorFlanco flipflopdsincronicoporflanco_1 (
    .D(and_1_out), .E(or_1_out), .Q(Salida[0]));  // open: NotQ
  FlipFlopDSincronicoPorFlanco flipflopdsincronicoporflanco_2 (
    .D(and_2_out), .E(or_1_out), .Q(Salida[1]));  // open: NotQ
  FlipFlopDSincronicoPorFlanco flipflopdsincronicoporflanco_3 (
    .D(and_3_out), .E(or_1_out), .Q(Salida[2]));  // open: NotQ
  FlipFlopDSincronicoPorFlanco flipflopdsincronicoporflanco_4 (
    .D(and_4_out), .E(or_1_out), .Q(Salida[3]));  // open: NotQ
  FlipFlopDSincronicoPorFlanco flipflopdsincronicoporflanco_5 (
    .D(and_5_out), .E(or_1_out), .Q(Salida[4]));  // open: NotQ
  FlipFlopDSincronicoPorFlanco flipflopdsincronicoporflanco_6 (
    .D(and_6_out), .E(or_1_out), .Q(Salida[5]));  // open: NotQ
  FlipFlopDSincronicoPorFlanco flipflopdsincronicoporflanco_7 (
    .D(and_7_out), .E(or_1_out), .Q(Salida[6]));  // open: NotQ
  FlipFlopDSincronicoPorFlanco flipflopdsincronicoporflanco_8 (
    .D(and_8_out), .E(or_1_out), .Q(Salida[7]));  // open: NotQ
  Hex_Digit_Display hex_digit_display_3 (.value(mostrardoshexa_2_digito2));  // open: dp
  MostrarDosHexa mostrardoshexa_2 (
    .Entrada(Salida), .Digito1(mostrardoshexa_2_digito1), .Digito2(mostrardoshexa_2_digito2));
  Hex_Digit_Display hex_digit_display_4 (.value(mostrardoshexa_2_digito1));  // open: dp
endmodule

module Acumulador8bit4 (
  input  ClockB,
  input  ClockA,
  input  [7:0] Dato,
  input  Reset,
  input  ResetA
);

  wire [7:0] latch8bits_1_salida, latch8bits_2_salida, sumador8bits_1_sum;

  Latch8bits latch8bits_1 (.Enable(ClockA), .Entrada(Dato), .Reset(ResetA), .Salida(latch8bits_1_salida));
  Sumador8bits sumador8bits_1 (
    .A(latch8bits_1_salida), .B(latch8bits_2_salida), .Sum(sumador8bits_1_sum));  // open: Cout
  Latch8bits latch8bits_2 (.Enable(ClockB), .Entrada(sumador8bits_1_sum), .Reset(Reset), .Salida(latch8bits_2_salida));
endmodule

module RestadorAcum8bit5 (
  input  Clock,
  input  Reset
);

  wire [7:0] latch8bits_1_salida, sumador8bits_1_sum;

  Sumador8bits sumador8bits_1 (.A({8{1'b1}}), .B(latch8bits_1_salida), .Sum(sumador8bits_1_sum));  // open: Cout
  Latch8bits latch8bits_1 (.Enable(Clock), .Entrada(sumador8bits_1_sum), .Reset(Reset), .Salida(latch8bits_1_salida));
endmodule

module RestadorAcum8bit6 (
  input  Clock,
  input  [7:0] in_2,
  input  Reset,
  input  in_4
);

  wire [7:0] latch8bits_1_salida, multiplexer_1_out, sumador8bits_1_sum;

  Sumador8bits sumador8bits_1 (.A({8{1'b1}}), .B(latch8bits_1_salida), .Sum(sumador8bits_1_sum));  // open: Cout
  Multiplexer #(.width(8)) multiplexer_1 (.in0(in_2), .in1(sumador8bits_1_sum), .out(multiplexer_1_out), .sel(in_4));
  Latch8bits latch8bits_1 (.Enable(Clock), .Entrada(multiplexer_1_out), .Reset(Reset), .Salida(latch8bits_1_salida));
endmodule

module Multiplicador8bit7 (
  input  [7:0] A,
  input  in_2,
  input  ClockA,
  input  ResetA,
  input  ClockB,
  input  [7:0] B,
  input  ResetB
);

  wire undriven;
  wire [7:0] latch8bits_1_salida, latch8bits_2_salida, register_1_q, sumador8bits_1_sum;

  Register register_1 (.D(A), .clk(ClockA), .Q(register_1_q), .clr(ResetA));  // open: en
  Latch8bits latch8bits_1 (.Enable(ClockB), .Entrada(B), .Reset(ResetB), .Salida(latch8bits_1_salida));
  Sumador8bits sumador8bits_1 (.A(register_1_q), .B(latch8bits_2_salida), .Sum(sumador8bits_1_sum));  // open: Cout
  Latch8bits latch8bits_2 (.Enable(undriven), .Entrada(sumador8bits_1_sum), .Reset(in_2), .Salida(latch8bits_2_salida));
endmodule

module Multiplicador8Bit7Definitivo (
  input  [7:0] A,
  input  in_2,
  input  in_3,
  input  [7:0] B
);

  wire and_1_out, and_2_out, Clock, Fin, not_1_out, or_1_out;
  wire [7:0] adder_1_out, adder_2_out, multiplexer_1_out, register_1_q, register_2_q, register_3_q;

  Clock clock_1 (.out(Clock));
  Register register_1 (.D(A), .clk(in_2), .Q(register_1_q), .clr(in_3));  // open: en
  Multiplexer #(.width(8)) multiplexer_1 (.in0(B), .in1(adder_1_out), .out(multiplexer_1_out), .sel(not_1_out));
  not not_1 (not_1_out, in_2);
  Adder adder_1 (.a({8{1'b1}}), .b(register_3_q), .out(adder_1_out));  // open: cin, cout
  Adder adder_2 (.a(register_1_q), .b(register_2_q), .out(adder_2_out));  // open: cin, cout
  and and_1 (and_1_out, Clock, ~Fin);  // AND_Gate
  nor nor_1 (Fin, multiplexer_1_out[0], multiplexer_1_out[1], multiplexer_1_out[2], multiplexer_1_out[3], multiplexer_1_out[4], multiplexer_1_out[5], multiplexer_1_out[6], multiplexer_1_out[7]);
  or or_1 (or_1_out, in_2, and_1_out);
  Register #(.trigger("falling")) register_2 (
    .D(adder_2_out), .clk(and_2_out), .Q(register_2_q), .clr(in_3));  // open: en
  and and_2 (and_2_out, Clock, ~Fin);  // AND_Gate
  Register #(.trigger("falling")) register_3 (
    .D(multiplexer_1_out), .clk(or_1_out), .Q(register_3_q), .clr(in_3));  // open: en

  // Other names for the same wires on the sheet: Calc = in_2; Reset = in_3
endmodule
