// Logisim project Tp4parte2.circ as structural Verilog
module Multiplicador8bitsDefinitivo (
  input  [7:0] A,
  input  in_2,
  input  in_3,
  input  [7:0] B
);

  wire and_1_out, and_2_out, Clock, Fin, not_1_out, or_1_out;
  wire [7:0] adder_1_out, adder_2_out, multiplexer_1_out, register_1_q, register_2_q, register_3_q;

  Clock clock_1 (.out(Clock));
  Register register_1 (.D(A), .clk(in_2), .Q(register_1_q), .clr(in_3));  // open: en
  Multiplexer #(.width(8)) multiplexer_1 (.in0(B), .in1(adder_1_out), .out(multiplexer_1_out), .sel(not_1_out));
  not not_1 (not_1_out, in_2);
  Adder adder_1 (.a({8{1'b1}}), .b(register_3_q), .out(adder_1_out));  // open: cin, cout
  Adder adder_2 (.a(register_1_q), .b(register_2_q), .out(adder_2_out));  // open: cin, cout
  and and_1 (and_1_out, Clock, ~Fin);  // AND_Gate
  or or_1 (or_1_out, in_2, and_1_out);
  Register #(.trigger("falling")) register_2 (
    .D(adder_2_out), .clk(and_2_out), .Q(register_2_q), .clr(in_3));  // open: en
  and and_2 (and_2_out, Clock, ~Fin);  // AND_Gate
  Register #(.trigger("falling")) register_3 (
    .D(multiplexer_1_out), .clk(or_1_out), .Q(register_3_q), .clr(in_3));  // open: en
  nor nor_1 (Fin, register_3_q[0], register_3_q[1], register_3_q[2], register_3_q[3], register_3_q[4], register_3_q[5], register_3_q[6], register_3_q[7]);

  // Other names for the same wires on the sheet: Reset = in_3; Set = in_2
endmodule
