// Logisim project temp.circ as structural Verilog: 1 circuit, main circuit main
module main (
  input  [1:0] A,
  input  [1:0] B,
  input  [3:0] in_3,
  output out_4,
  output S0,
  output S1
);

  wire nand_1_out, nand_2_out, nand_3_out, nand_4_out, nand_5_out, nand_6_out, nand_7_out, nand_8_out,
       nand_9_out, nand_10_out, nand_11_out, nand_12_out, nand_13_out, nand_14_out, nand_16_out, nand_17_out,
       nand_18_out, nand_19_out, nand_20_out, nand_21_out, nand_22_out, nand_23_out, nand_24_out,
       nand_25_out, nand_26_out, nand_27_out, nand_28_out, nand_29_out, nand_30_out, nand_31_out,
       nand_32_out, nand_33_out, nand_34_out, nand_35_out, nand_36_out, nand_37_out;

  nand nand_1 (nand_1_out, A[1], A[1]);
  nand nand_2 (nand_2_out, A[0], A[0]);
  nand nand_3 (nand_3_out, B[1], B[1]);
  nand nand_4 (nand_4_out, B[0], B[0]);
  nand nand_5 (nand_5_out, nand_4_out, A[0]);
  nand nand_6 (nand_6_out, nand_2_out, B[0]);
  nand nand_7 (nand_7_out, A[1], nand_3_out);
  nand nand_8 (nand_8_out, A[1], nand_2_out);
  nand nand_9 (nand_9_out, nand_2_out, nand_1_out);
  nand nand_10 (nand_10_out, nand_1_out, B[1]);
  nand nand_11 (nand_11_out, nand_1_out, A[0]);
  nand nand_12 (nand_12_out, nand_3_out, B[0]);
  nand nand_13 (nand_13_out, A[1], A[0]);
  nand nand_14 (nand_14_out, B[1], B[0]);
  nand nand_15 (S0, nand_5_out, nand_6_out);
  nand nand_16 (nand_16_out, nand_7_out, nand_7_out);
  nand nand_17 (nand_17_out, nand_8_out, nand_8_out);
  nand nand_18 (nand_18_out, nand_9_out, nand_9_out);
  nand nand_19 (nand_19_out, nand_10_out, nand_10_out);
  nand nand_20 (nand_20_out, nand_11_out, nand_11_out);
  nand nand_21 (nand_21_out, nand_12_out, nand_12_out);
  nand nand_22 (nand_22_out, nand_13_out, nand_13_out);
  nand nand_23 (nand_23_out, nand_14_out, nand_14_out);
  nand nand_24 (nand_24_out, nand_16_out, nand_4_out);
  nand nand_25 (nand_25_out, nand_17_out, nand_3_out);
  nand nand_26 (nand_26_out, nand_18_out, B[1]);
  nand nand_27 (nand_27_out, nand_19_out, nand_4_out);
  nand nand_28 (nand_28_out, nand_20_out, nand_21_out);
  nand nand_29 (nand_29_out, nand_22_out, nand_23_out);
  nand nand_30 (nand_30_out, nand_24_out, nand_25_out);
  nand nand_31 (nand_31_out, nand_26_out, nand_27_out);
  nand nand_32 (nand_32_out, nand_28_out, nand_29_out);
  nand nand_33 (nand_33_out, nand_30_out, nand_30_out);
  nand nand_34 (nand_34_out, nand_31_out, nand_31_out);
  nand nand_35 (nand_35_out, nand_32_out, nand_32_out);
  nand nand_36 (nand_36_out, nand_33_out, nand_34_out);
  Multiplexer #(.select(4)) multiplexer_1 (
    .in12(1'b1), .out(out_4), .sel(in_3));  // open: in0, in1, in2, in3, in4, in5, in6, in7, in8, in9, in10, in11, in13, in14, in15
  nand nand_37 (nand_37_out, nand_36_out, nand_36_out);
  nand nand_38 (S1, nand_37_out, nand_35_out);
endmodule
