// Logisim project tp4parte3.circ as structural Verilog: 15 circuits, main circuit main
module main (
  input  [7:0] Paralelo,
  input  Latch,
  input  Clock,
  output [7:0] Salida
);

  wire paraleloserie_1_serie;

  ParaleloSerie paraleloserie_1 (.Paralelo(Paralelo), .Latch(Latch), .Clock(Clock), .Serie(paraleloserie_1_serie));
  SerieParalelo serieparalelo_1 (.Serie(paraleloserie_1_serie), .Clock(Clock), .Paralelo(Salida));
endmodule

module ParaleloSerie (
  input  [7:0] Paralelo,
  input  Latch,
  input  Clock,
  output Serie
);

  wire and_1_out;
  wire [7:0] d_ff_8_q;

  and and_1 (and_1_out, Latch, Clock);
  D_Flip_Flop d_ff_1 (.D(Paralelo[7]), .clk(and_1_out), .Q(d_ff_8_q[7]));  // open: Qn, preset, reset
  D_Flip_Flop d_ff_2 (.D(Paralelo[6]), .clk(and_1_out), .Q(d_ff_8_q[6]));  // open: Qn, preset, reset
  D_Flip_Flop d_ff_3 (.D(Paralelo[5]), .clk(and_1_out), .Q(d_ff_8_q[5]));  // open: Qn, preset, reset
  D_Flip_Flop d_ff_4 (.D(Paralelo[4]), .clk(and_1_out), .Q(d_ff_8_q[4]));  // open: Qn, preset, reset
  D_Flip_Flop d_ff_5 (.D(Paralelo[3]), .clk(and_1_out), .Q(d_ff_8_q[3]));  // open: Qn, preset, reset
  D_Flip_Flop d_ff_6 (.D(Paralelo[2]), .clk(and_1_out), .Q(d_ff_8_q[2]));  // open: Qn, preset, reset
  D_Flip_Flop d_ff_7 (.D(Paralelo[1]), .clk(and_1_out), .Q(d_ff_8_q[1]));  // open: Qn, preset, reset
  D_Flip_Flop d_ff_8 (.D(Paralelo[0]), .clk(and_1_out), .Q(d_ff_8_q[0]));  // open: Qn, preset, reset
  Contador contador_1 (.D(d_ff_8_q), .Clock(Clock), .Latch(Latch), .Serie(Serie));
endmodule

module SerieParalelo (
  input  Serie,
  input  Clock,
  output [7:0] Paralelo
);

  D_Flip_Flop d_ff_1 (.D(Serie), .clk(Clock), .Q(Paralelo[7]));  // open: Qn, preset, reset
  D_Flip_Flop d_ff_2 (.D(Paralelo[7]), .clk(Clock), .Q(Paralelo[6]));  // open: Qn, preset, reset
  D_Flip_Flop d_ff_3 (.D(Paralelo[6]), .clk(Clock), .Q(Paralelo[5]));  // open: Qn, preset, reset
  D_Flip_Flop d_ff_4 (.D(Paralelo[5]), .clk(Clock), .Q(Paralelo[4]));  // open: Qn, preset, reset
  D_Flip_Flop d_ff_5 (.D(Paralelo[4]), .clk(Clock), .Q(Paralelo[3]));  // open: Qn, preset, reset
  D_Flip_Flop d_ff_6 (.D(Paralelo[3]), .clk(Clock), .Q(Paralelo[2]));  // open: Qn, preset, reset
  D_Flip_Flop d_ff_7 (.D(Paralelo[2]), .clk(Clock), .Q(Paralelo[1]));  // open: Qn, preset, reset
  D_Flip_Flop d_ff_8 (.D(Paralelo[1]), .clk(Clock), .Q(Paralelo[0]));  // open: Qn, preset, reset
endmodule

module Contador (
  input  [7:0] D,
  input  Clock,
  input  Latch,
  output Serie
);

  wire and_1_out, d_ff_1_q, d_ff_2_q, d_ff_3_q, d_ff_4_q, d_ff_5_q, d_ff_6_q, d_ff_7_q, multiplexer_1_out,
       multiplexer_2_out, multiplexer_3_out, multiplexer_4_out, multiplexer_5_out, multiplexer_6_out,
       multiplexer_7_out, multiplexer_8_out, not_1_out;

  and and_1 (and_1_out, Serie, 1'b0);
  not not_1 (not_1_out, Latch);
  D_Flip_Flop d_ff_1 (.D(multiplexer_1_out), .clk(Clock), .Q(d_ff_1_q));  // open: Qn, preset, reset
  Multiplexer multiplexer_1 (.in0(D[7]), .in1(and_1_out), .out(multiplexer_1_out), .sel(not_1_out));
  D_Flip_Flop d_ff_2 (.D(multiplexer_2_out), .clk(Clock), .Q(d_ff_2_q));  // open: Qn, preset, reset
  Multiplexer multiplexer_2 (.in0(D[6]), .in1(d_ff_1_q), .out(multiplexer_2_out), .sel(not_1_out));
  D_Flip_Flop d_ff_3 (.D(multiplexer_3_out), .clk(Clock), .Q(d_ff_3_q));  // open: Qn, preset, reset
  Multiplexer multiplexer_3 (.in0(D[5]), .in1(d_ff_2_q), .out(multiplexer_3_out), .sel(not_1_out));
  D_Flip_Flop d_ff_4 (.D(multiplexer_4_out), .clk(Clock), .Q(d_ff_4_q));  // open: Qn, preset, reset
  Multiplexer multiplexer_4 (.in0(D[4]), .in1(d_ff_3_q), .out(multiplexer_4_out), .sel(not_1_out));
  Multiplexer multiplexer_5 (.in0(D[3]), .in1(d_ff_4_q), .out(multiplexer_5_out), .sel(not_1_out));
  D_Flip_Flop d_ff_5 (.D(multiplexer_5_out), .clk(Clock), .Q(d_ff_5_q));  // open: Qn, preset, reset
  D_Flip_Flop d_ff_6 (.D(multiplexer_6_out), .clk(Clock), .Q(d_ff_6_q));  // open: Qn, preset, reset
  Multiplexer multiplexer_6 (.in0(D[2]), .in1(d_ff_5_q), .out(multiplexer_6_out), .sel(not_1_out));
  D_Flip_Flop d_ff_7 (.D(multiplexer_7_out), .clk(Clock), .Q(d_ff_7_q));  // open: Qn, preset, reset
  Multiplexer multiplexer_7 (.in0(D[1]), .in1(d_ff_6_q), .out(multiplexer_7_out), .sel(not_1_out));
  D_Flip_Flop d_ff_8 (.D(multiplexer_8_out), .clk(Clock), .Q(Serie));  // open: Qn, preset, reset
  Multiplexer multiplexer_8 (.in0(D[0]), .in1(d_ff_7_q), .out(multiplexer_8_out), .sel(not_1_out));
endmodule

module CBASMod16DescE09 (
  input  Clock,
  output [2:0] out_2
);

  T_Flip_Flop t_ff_1 (.T(1'b1), .clk(Clock), .Q(out_2[0]));  // open: Qn, reset, preset
  T_Flip_Flop t_ff_2 (.T(1'b1), .clk(out_2[0]), .Q(out_2[1]));  // open: Qn, reset, preset
  // Digital_Oscilloscope digital_oscilloscope_1: pin names not known; wires that end beside it: Clock, out_2[0], out_2[1], out_2[2]
  T_Flip_Flop t_ff_3 (.T(1'b1), .clk(out_2[1]), .Q(out_2[2]));  // open: Qn, reset, preset

  // Notes on the sheet:
  //   Lol, mod16 requiere de un latch mas
endmodule

module CBSMod16AscE10 (
  input  Clock,
  output [3:0] Salida
);

  wire and_1_out, and_2_out;

  T_Flip_Flop #(.trigger("falling")) t_ff_1 (.T(1'b1), .clk(Clock), .Q(Salida[0]));  // open: Qn, reset, preset
  T_Flip_Flop #(.trigger("falling")) t_ff_2 (.T(Salida[0]), .clk(Clock), .Q(Salida[1]));  // open: Qn, reset, preset
  and and_1 (and_1_out, Salida[0], Salida[1]);
  T_Flip_Flop #(.trigger("falling")) t_ff_3 (.T(and_1_out), .clk(Clock), .Q(Salida[2]));  // open: Qn, reset, preset
  and and_2 (and_2_out, Salida[0], Salida[1], Salida[2]);
  T_Flip_Flop #(.trigger("falling")) t_ff_4 (.T(and_2_out), .clk(Clock), .Q(Salida[3]));  // open: Qn, reset, preset
endmodule

module CJohnsonMod10E11 (
  input  Clock,
  output [4:0] Johnson
);

  wire not_1_out;

  not not_1 (not_1_out, Johnson[0]);
  D_Flip_Flop d_ff_1 (.D(not_1_out), .clk(Clock), .Q(Johnson[4]));  // open: Qn, preset, reset
  D_Flip_Flop d_ff_2 (.D(Johnson[4]), .clk(Clock), .Q(Johnson[3]));  // open: Qn, preset, reset
  D_Flip_Flop d_ff_3 (.D(Johnson[3]), .clk(Clock), .Q(Johnson[2]));  // open: Qn, preset, reset
  D_Flip_Flop d_ff_4 (.D(Johnson[2]), .clk(Clock), .Q(Johnson[1]));  // open: Qn, preset, reset
  D_Flip_Flop d_ff_5 (.D(Johnson[1]), .clk(Clock), .Q(Johnson[0]));  // open: Qn, preset, reset
endmodule

module COneHotMod5E12 (
  input  Clock,
  output [4:0] OneHot
);

  wire por_1_out;

  POR por_1 (.out(por_1_out));
  D_Flip_Flop d_ff_1 (.D(OneHot[0]), .clk(Clock), .Q(OneHot[4]), .preset(por_1_out));  // open: Qn, reset
  D_Flip_Flop d_ff_2 (.D(OneHot[4]), .clk(Clock), .Q(OneHot[3]));  // open: Qn, preset, reset
  D_Flip_Flop d_ff_3 (.D(OneHot[3]), .clk(Clock), .Q(OneHot[2]));  // open: Qn, preset, reset
  D_Flip_Flop d_ff_4 (.D(OneHot[2]), .clk(Clock), .Q(OneHot[1]));  // open: Qn, preset, reset
  D_Flip_Flop d_ff_5 (.D(OneHot[1]), .clk(Clock), .Q(OneHot[0]));  // open: Qn, preset, reset
endmodule

module ContadorMod60E13 (
  input  Clock,
  output [3:0] C1,
  output [3:0] C0,
  output Carry
);

  wire contadormod10e13_1_carry;

  ContadorMod6E13 contadormod6e13_1 (.Clock(contadormod10e13_1_carry), .Salida(C1), .Carry(Carry));
  ContadorMod10E13 contadormod10e13_1 (.Clock(Clock), .Salida(C0), .Carry(contadormod10e13_1_carry));
endmodule

module ContadorMod10E13 (
  input  Clock,
  output [3:0] Salida,
  output Carry
);

  wire and_2_out, and_3_out;

  T_Flip_Flop #(.trigger("falling")) t_ff_1 (.T(1'b1), .clk(Clock), .Q(Salida[0]), .reset(Carry));  // open: Qn, preset
  and and_1 (Carry, ~Salida[0], Salida[1], ~Salida[2], Salida[3]);  // AND_Gate
  T_Flip_Flop #(.trigger("falling")) t_ff_2 (
    .T(Salida[0]), .clk(Clock), .Q(Salida[1]), .reset(Carry));  // open: Qn, preset
  and and_2 (and_2_out, Salida[0], Salida[1]);
  T_Flip_Flop #(.trigger("falling")) t_ff_3 (
    .T(and_2_out), .clk(Clock), .Q(Salida[2]), .reset(Carry));  // open: Qn, preset
  and and_3 (and_3_out, Salida[0], Salida[1], Salida[2]);
  T_Flip_Flop #(.trigger("falling")) t_ff_4 (
    .T(and_3_out), .clk(Clock), .Q(Salida[3]), .reset(Carry));  // open: Qn, preset
endmodule

module ContadorMod6E13 (
  input  Clock,
  output [3:0] Salida,
  output Carry
);

  wire and_2_out, and_3_out;

  T_Flip_Flop #(.trigger("falling")) t_ff_1 (.T(1'b1), .clk(Clock), .Q(Salida[0]), .reset(Carry));  // open: Qn, preset
  and and_1 (Carry, ~Salida[0], Salida[1], Salida[2], ~Salida[3]);  // AND_Gate
  T_Flip_Flop #(.trigger("falling")) t_ff_2 (
    .T(Salida[0]), .clk(Clock), .Q(Salida[1]), .reset(Carry));  // open: Qn, preset
  and and_2 (and_2_out, Salida[0], Salida[1]);
  T_Flip_Flop #(.trigger("falling")) t_ff_3 (
    .T(and_2_out), .clk(Clock), .Q(Salida[2]), .reset(Carry));  // open: Qn, preset
  and and_3 (and_3_out, Salida[0], Salida[1], Salida[2]);
  T_Flip_Flop #(.trigger("falling")) t_ff_4 (
    .T(and_3_out), .clk(Clock), .Q(Salida[3]), .reset(Carry));  // open: Qn, preset
endmodule

module ContadorRelojE14 (
);

  wire clock_1_out, contadormod60e13_1_carry, contadormod60e13_2_carry;
  wire [1:0] contadormod24e14_1_c1;
  wire [3:0] contadormod24e14_1_c0, contadormod60e13_1_c0, contadormod60e13_1_c1, contadormod60e13_2_c0,
       contadormod60e13_2_c1;

  Clock clock_1 (.out(clock_1_out));
  ContadorMod60E13 contadormod60e13_1 (
    .Clock(clock_1_out), .C1(contadormod60e13_1_c1), .C0(contadormod60e13_1_c0),
    .Carry(contadormod60e13_1_carry));
  ContadorMod60E13 contadormod60e13_2 (
    .Clock(contadormod60e13_1_carry), .C1(contadormod60e13_2_c1), .C0(contadormod60e13_2_c0),
    .Carry(contadormod60e13_2_carry));
  ContadorMod24E14 contadormod24e14_1 (
    .Clock(contadormod60e13_2_carry), .C1(contadormod24e14_1_c1), .C0(contadormod24e14_1_c0));
  Hex_Digit_Display hex_digit_display_1 (.value({2'b00, contadormod24e14_1_c1}));  // open: dp
  Hex_Digit_Display hex_digit_display_2 (.value(contadormod24e14_1_c0));  // open: dp
  Hex_Digit_Display hex_digit_display_3 (.value(contadormod60e13_2_c0));  // open: dp
  Hex_Digit_Display hex_digit_display_4 (.value(contadormod60e13_2_c1));  // open: dp
  Hex_Digit_Display hex_digit_display_5 (.value(contadormod60e13_1_c1));  // open: dp
  Hex_Digit_Display hex_digit_display_6 (.value(contadormod60e13_1_c0));  // open: dp
endmodule

module ContadorMod24E14 (
  input  Clock,
  output [1:0] C1,
  output [3:0] C0
);

  wire and_1_out, contadormod10resete14_1_carry;

  and and_1 (and_1_out, C1[1], ~C1[0], ~C0[3], C0[2], ~C0[1], ~C0[0]);  // AND_Gate
  ContadorMod3E14 contadormod3e14_1 (.Clock(contadormod10resete14_1_carry), .Reset(and_1_out), .Salida(C1));
  ContadorMod10ResetE14 contadormod10resete14_1 (
    .Clock(Clock), .Reset(and_1_out), .Salida(C0), .Carry(contadormod10resete14_1_carry));
endmodule

module ContadorMod3E14 (
  input  Clock,
  input  Reset,
  output [1:0] Salida
);

  wire and_1_out, or_1_out;

  T_Flip_Flop t_ff_1 (.T(1'b1), .clk(Clock), .Q(Salida[0]), .reset(or_1_out));  // open: Qn, preset
  or or_1 (or_1_out, Reset, and_1_out);
  and and_1 (and_1_out, Salida[0], Salida[1]);
  T_Flip_Flop t_ff_2 (.T(Salida[0]), .clk(Clock), .Q(Salida[1]), .reset(or_1_out));  // open: Qn, preset
endmodule

module ContadorMod10ResetE14 (
  input  Clock,
  input  Reset,
  output [3:0] Salida,
  output Carry
);

  wire and_2_out, and_3_out, or_1_out;

  T_Flip_Flop #(.trigger("falling")) t_ff_1 (
    .T(1'b1), .clk(Clock), .Q(Salida[0]), .reset(or_1_out));  // open: Qn, preset
  or or_1 (or_1_out, Reset, Carry);
  and and_1 (Carry, ~Salida[0], Salida[1], ~Salida[2], Salida[3]);  // AND_Gate
  T_Flip_Flop #(.trigger("falling")) t_ff_2 (
    .T(Salida[0]), .clk(Clock), .Q(Salida[1]), .reset(or_1_out));  // open: Qn, preset
  and and_2 (and_2_out, Salida[0], Salida[1]);
  T_Flip_Flop #(.trigger("falling")) t_ff_3 (
    .T(and_2_out), .clk(Clock), .Q(Salida[2]), .reset(or_1_out));  // open: Qn, preset
  and and_3 (and_3_out, Salida[0], Salida[1], Salida[2]);
  T_Flip_Flop #(.trigger("falling")) t_ff_4 (
    .T(and_3_out), .clk(Clock), .Q(Salida[3]), .reset(or_1_out));  // open: Qn, preset
endmodule
